// Digital circuit ALU.dig as structural Verilog
module ALU (
  input  [7:0] A,
  input  [7:0] B,
  input  [3:0] S,
  input  CI,
  input  SOE,
  input  DOE,
  input  FOE,
  output [7:0] O,
  output ALUDF
);

  wire not_1_out, not_2_out;
  wire [6:2] alud_1_ac;

  not not_1 (not_1_out, DOE);
  not not_2 (not_2_out, SOE);
  ALUD alud_1 (.CI(CI), .A(A), .B(B), .S(S), .nOE(not_1_out), .Q(O), .CO(ALUDF), .AC(alud_1_ac[6]), .OV(alud_1_ac[2]));
  EEPROM #(.AddrBits(13), .isProgramMemory("true"), .Bits(8)) ALUS (
    .A({CI, S, A}), .CS(~1'b0), .WE(~1'b1), .OE(~not_2_out), .D(O));
  assign O = FOE ? {ALUDF, alud_1_ac[6], 3'b111, alud_1_ac[2], 2'b11} : 8'bz;  // Driver driver_1

  // Notes on the sheet:
  //   contents of ALUS (hex, n*v repeats v):
  //   0,1,2,3,4,5,6,7,8,9,a,b,c,d,e,f,10,11,12,13,14,15,16,17,18,19,1a,1b,1c,1d,1e,1f,20,
  //   21,22,23,24,25,26,27,28,29,2a,2b,2c,2d,2e,2f,30,31,32,33,34,35,36,37,38,39,3a,3b,
  //   3c,3d,3e,3f,40,41,42,43,44,45,46,47,48,49,4a,4b,4c,4d,4e,4f,50,51,52,53,54,55,56,
  //   57,58,59,5a,5b,5c,5d,5e,5f,60,61,62,63,64,65,66,67,68,69,6a,6b,6c,6d,6e,6f,70,71,
  //   72,73,74,75,76,77,78,79,7a,7b,7c,7d,7e,7f,80,81,82,83,84,85,86,87,88,89,8a,8b,8c,
  //   8d,8e,8f,90,91,92,93,94,95,96,97,98,99,9a,9b,9c,9d,9e,9f,a0,a1,a2,a3,a4,a5,a6,a7,
  //   a8,a9,aa,ab,ac,ad,ae,af,b0,b1,b2,b3,b4,b5,b6,b7,b8,b9,ba,bb,bc,bd,be,bf,c0,c1,c2,
  //   c3,c4,c5,c6,c7,c8,c9,ca,cb,cc,cd,ce,cf,d0,d1,d2,d3,d4,d5,d6,d7,d8,d9,da,db,dc,dd,
  //   de,df,e0,e1,e2,e3,e4,e5,e6,e7,e8,e9,ea,eb,ec,ed,ee,ef,f0,f1,f2,f3,f4,f5,f6,f7,f8,
  //   f9,fa,fb,fc,fd,fe,ff,ff,fe,fd,fc,fb,fa,f9,f8,f7,f6,f5,f4,f3,f2,f1,f0,ef,ee,ed,ec,
  //   eb,ea,e9,e8,e7,e6,e5,e4,e3,e2,e1,e0,df,de,dd,dc,db,da,d9,d8,d7,d6,d5,d4,d3,d2,d1,
  //   d0,cf,ce,cd,cc,cb,ca,c9,c8,c7,c6,c5,c4,c3,c2,c1,c0,bf,be,bd,bc,bb,ba,b9,b8,b7,b6,
  //   b5,b4,b3,b2,b1,b0,af,ae,ad,ac,ab,aa,a9,a8,a7,a6,a5,a4,a3,a2,a1,a0,9f,9e,9d,9c,9b,
  //   9a,99,98,97,96,95,94,93,92,91,90,8f,8e,8d,8c,8b,8a,89,88,87,86,85,84,83,82,81,80,
  //   7f,7e,7d,7c,7b,7a,79,78,77,76,75,74,73,72,71,70,6f,6e,6d,6c,6b,6a,69,68,67,66,65,
  //   64,63,62,61,60,5f,5e,5d,5c,5b,5a,59,58,57,56,55,54,53,52,51,50,4f,4e,4d,4c,4b,4a,
  //   49,48,47,46,45,44,43,42,41,40,3f,3e,3d,3c,3b,3a,39,38,37,36,35,34,33,32,31,30,2f,
  //   2e,2d,2c,2b,2a,29,28,27,26,25,24,23,22,21,20,1f,1e,1d,1c,1b,1a,19,18,17,16,15,14,
  //   13,12,11,10,f,e,d,c,b,a,9,8,7,6,5,4,3,2,1,0,0,0,0,0,0,0,0,0,0,0,0,0,0,0,0,0,0,0,0,
  //   0,0,0,0,0,0,0,0,0,0,0,0,0,0,0,0,0,0,0,0,0,0,0,0,0,0,0,0,0,0,0,0,0,0,0,0,0,0,0,0,0,
  //   0,0,0,0,0,0,0,0,0,0,0,0,0,0,0,0,0,0,0,0,0,0,0,0,0,0,0,0,0,0,0,0,0,0,0,0,0,0,0,0,0,
  //   0,0,0,0,0,0,0,0,0,0,0,0,0,0,0,0,0,0,0,0,0,0,0,0,0,0,0,0,0,0,0,0,0,0,0,0,0,0,0,0,0,
  //   0,0,0,0,0,0,0,0,0,0,0,0,0,0,0,0,0,0,0,0,0,0,0,0,0,0,0,0,0,0,0,0,0,0,0,0,0,0,0,0,0,
  //   0,0,0,0,0,0,0,0,0,0,0,0,0,0,0,0,0,0,0,0,0,0,0,0,0,0,0,0,0,0,0,0,0,0,0,0,0,0,0,0,0,
  //   0,0,0,0,0,0,0,0,0,0,0,0,0,0,0,0,0,0,0,0,0,0,0,0,0,0,0,0,0,0,0,0,0,0,2,2,4,4,6,6,8,
  //   8,a,a,c,c,e,e,10,10,12,12,14,14,16,16,18,18,1a,1a,1c,1c,1e,1e,20,20,22,22,24,24,26,
  //   26,28,28,2a,2a,2c,2c,2e,2e,30,30,32,32,34,34,36,36,38,38,3a,3a,3c,3c,3e,3e,40,40,
  //   42,42,44,44,46,46,48,48,4a,4a,4c,4c,4e,4e,50,50,52,52,54,54,56,56,58,58,5a,5a,5c,
  //   5c,5e,5e,60,60,62,62,64,64,66,66,68,68,6a,6a,6c,6c,6e,6e,70,70,72,72,74,74,76,76,
  //   78,78,7a,7a,7c,7c,7e,7e,80,80,82,82,84,84,86,86,88,88,8a,8a,8c,8c,8e,8e,90,90,92,
  //   92,94,94,96,96,98,98,9a,9a,9c,9c,9e,9e,a0,a0,a2,a2,a4,a4,a6,a6,a8,a8,aa,aa,ac,ac,
  //   ae,ae,b0,b0,b2,b2,b4,b4,b6,b6,b8,b8,ba,ba,bc,bc,be,be,c0,c0,c2,c2,c4,c4,c6,c6,c8,
  //   c8,ca,ca,cc,cc,ce,ce,d0,d0,d2,d2,d4,d4,d6,d6,d8,d8,da,da,dc,dc,de,de,e0,e0,e2,e2,
  //   e4,e4,e6,e6,e8,e8,ea,ea,ec,ec,ee,ee,f0,f0,f2,f2,f4,f4,f6,f6,f8,f8,fa,fa,fc,fc,fe,
  //   fe,0,80,1,81,2,82,3,83,4,84,5,85,6,86,7,87,8,88,9,89,a,8a,b,8b,c,8c,d,8d,e,8e,f,8f,
  //   10,90,11,91,12,92,13,93,14,94,15,95,16,96,17,97,18,98,19,99,1a,9a,1b,9b,1c,9c,1d,
  //   9d,1e,9e,1f,9f,20,a0,21,a1,22,a2,23,a3,24,a4,25,a5,26,a6,27,a7,28,a8,29,a9,2a,aa,
  //   2b,ab,2c,ac,2d,ad,2e,ae,2f,af,30,b0,31,b1,32,b2,33,b3,34,b4,35,b5,36,b6,37,b7,38,
  //   b8,39,b9,3a,ba,3b,bb,3c,bc,3d,bd,3e,be,3f,bf,40,c0,41,c1,42,c2,43,c3,44,c4,45,c5,
  //   46,c6,47,c7,48,c8,49,c9,4a,ca,4b,cb,4c,cc,4d,cd,4e,ce,4f,cf,50,d0,51,d1,52,d2,53,
  //   d3,54,d4,55,d5,56,d6,57,d7,58,d8,59,d9,5a,da,5b,db,5c,dc,5d,dd,5e,de,5f,df,60,e0,
  //   61,e1,62,e2,63,e3,64,e4,65,e5,66,e6,67,e7,68,e8,69,e9,6a,ea,6b,eb,6c,ec,6d,ed,6e,
  //   ee,6f,ef,70,f0,71,f1,72,f2,73,f3,74,f4,75,f5,76,f6,77,f7,78,f8,79,f9,7a,fa,7b,fb,
  //   7c,fc,7d,fd,7e,fe,7f,ff,0,2,4,6,8,a,c,e,10,12,14,16,18,1a,1c,1e,20,22,24,26,28,2a,
  //   2c,2e,30,32,34,36,38,3a,3c,3e,40,42,44,46,48,4a,4c,4e,50,52,54,56,58,5a,5c,5e,60,
  //   62,64,66,68,6a,6c,6e,70,72,74,76,78,7a,7c,7e,80,82,84,86,88,8a,8c,8e,90,92,94,96,
  //   98,9a,9c,9e,a0,a2,a4,a6,a8,aa,ac,ae,b0,b2,b4,b6,b8,ba,bc,be,c0,c2,c4,c6,c8,ca,cc,
  //   ce,d0,d2,d4,d6,d8,da,dc,de,e0,e2,e4,e6,e8,ea,ec,ee,f0,f2,f4,f6,f8,fa,fc,fe,1,3,5,
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endmodule
