// Digital circuit ALUD.dig as structural Verilog
module ALUD (
  input  CI,
  input  [7:0] A,
  input  [7:0] B,
  input  [3:0] S,
  input  nOE,
  output [7:0] Q,
  output CO,
  output AC,
  output OV
);

  wire [7:4] ALUDH_d, ALUDL_d;

  EEPROM #(.AddrBits(13), .isProgramMemory("true"), .Bits(8)) ALUDL (
    .A({CI, S, B[3:0], A[3:0]}), .CS(~1'b0), .WE(~1'b1), .OE(~nOE), .D({ALUDL_d[7], AC, ALUDL_d[5:4], Q[3:0]}));
  EEPROM #(.AddrBits(13), .isProgramMemory("true"), .Bits(8)) ALUDH (
    .A({AC, S, B[7:4], A[7:4]}), .CS(~1'b0), .WE(~1'b1), .OE(~nOE),
    .D({ALUDH_d[7], CO, OV, ALUDH_d[4], Q[7:4]}));

  // Notes on the sheet:
  //   contents of ALUDL (hex, n*v repeats v):
  //   0,1,2,3,4,5,6,7,8,9,a,b,c,d,e,f,1,1,3,3,5,5,7,7,9,9,b,b,d,d,f,f,2,3,2,3,6,7,6,7,a,
  //   b,a,b,e,f,e,f,3,3,3,3,7,7,7,7,b,b,b,b,f,f,f,f,4,5,6,7,4,5,6,7,c,d,e,f,c,d,e,f,5,5,
  //   7,7,5,5,7,7,d,d,f,f,d,d,f,f,6,7,6,7,6,7,6,7,e,f,e,f,e,f,e,f,7,7,7,7,7,7,7,7,f,f,f,
  //   f,f,f,f,f,8,9,a,b,c,d,e,f,8,9,a,b,c,d,e,f,9,9,b,b,d,d,f,f,9,9,b,b,d,d,f,f,a,b,a,b,
  //   e,f,e,f,a,b,a,b,e,f,e,f,b,b,b,b,f,f,f,f,b,b,b,b,f,f,f,f,c,d,e,f,c,d,e,f,c,d,e,f,c,
  //   d,e,f,d,d,f,f,d,d,f,f,d,d,f,f,d,d,f,f,e,f,e,f,e,f,e,f,e,f,e,f,e,f,e,f,f,f,f,f,f,f,
  //   f,f,f,f,f,f,f,f,f,f,0,0,0,0,0,0,0,0,0,0,0,0,0,0,0,0,0,1,0,1,0,1,0,1,0,1,0,1,0,1,0,
  //   1,0,0,2,2,0,0,2,2,0,0,2,2,0,0,2,2,0,1,2,3,0,1,2,3,0,1,2,3,0,1,2,3,0,0,0,0,4,4,4,4,
  //   0,0,0,0,4,4,4,4,0,1,0,1,4,5,4,5,0,1,0,1,4,5,4,5,0,0,2,2,4,4,6,6,0,0,2,2,4,4,6,6,0,
  //   1,2,3,4,5,6,7,0,1,2,3,4,5,6,7,0,0,0,0,0,0,0,0,8,8,8,8,8,8,8,8,0,1,0,1,0,1,0,1,8,9,
  //   8,9,8,9,8,9,0,0,2,2,0,0,2,2,8,8,a,a,8,8,a,a,0,1,2,3,0,1,2,3,8,9,a,b,8,9,a,b,0,0,0,
  //   0,4,4,4,4,8,8,8,8,c,c,c,c,0,1,0,1,4,5,4,5,8,9,8,9,c,d,c,d,0,0,2,2,4,4,6,6,8,8,a,a,
  //   c,c,e,e,0,1,2,3,4,5,6,7,8,9,a,b,c,d,e,f,0,1,2,3,4,5,6,7,8,9,a,b,c,d,e,f,1,0,3,2,5,
  //   4,7,6,9,8,b,a,d,c,f,e,2,3,0,1,6,7,4,5,a,b,8,9,e,f,c,d,3,2,1,0,7,6,5,4,b,a,9,8,f,e,
  //   d,c,4,5,6,7,0,1,2,3,c,d,e,f,8,9,a,b,5,4,7,6,1,0,3,2,d,c,f,e,9,8,b,a,6,7,4,5,2,3,0,
  //   1,e,f,c,d,a,b,8,9,7,6,5,4,3,2,1,0,f,e,d,c,b,a,9,8,8,9,a,b,c,d,e,f,0,1,2,3,4,5,6,7,
  //   9,8,b,a,d,c,f,e,1,0,3,2,5,4,7,6,a,b,8,9,e,f,c,d,2,3,0,1,6,7,4,5,b,a,9,8,f,e,d,c,3,
  //   2,1,0,7,6,5,4,c,d,e,f,8,9,a,b,4,5,6,7,0,1,2,3,d,c,f,e,9,8,b,a,5,4,7,6,1,0,3,2,e,f,
  //   c,d,a,b,8,9,6,7,4,5,2,3,0,1,f,e,d,c,b,a,9,8,7,6,5,4,3,2,1,0,0,0,0,0,0,0,0,0,0,0,0,
  //   0,0,0,0,0,1,1,1,1,1,1,1,1,1,1,1,1,1,1,1,1,2,2,2,2,2,2,2,2,2,2,2,2,2,2,2,2,3,3,3,3,
  //   3,3,3,3,3,3,3,3,3,3,3,3,4,4,4,4,4,4,4,4,4,4,4,4,4,4,4,4,5,5,5,5,5,5,5,5,5,5,5,5,5,
  //   5,5,5,6,6,6,6,6,6,6,6,6,6,6,6,6,6,6,6,7,7,7,7,7,7,7,7,7,7,7,7,7,7,7,7,8,8,8,8,8,8,
  //   8,8,8,8,8,8,8,8,8,8,9,9,9,9,9,9,9,9,9,9,9,9,9,9,9,9,a,a,a,a,a,a,a,a,a,a,a,a,a,a,a,
  //   a,b,b,b,b,b,b,b,b,b,b,b,b,b,b,b,b,c,c,c,c,c,c,c,c,c,c,c,c,c,c,c,c,d,d,d,d,d,d,d,d,
  //   d,d,d,d,d,d,d,d,e,e,e,e,e,e,e,e,e,e,e,e,e,e,e,e,f,f,f,f,f,f,f,f,f,f,f,f,f,f,f,f,0,
  //   1,2,3,4,5,6,7,8,9,a,b,c,d,e,f,1,2,3,4,5,6,7,48,9,a,b,c,d,e,f,80,2,3,4,5,6,7,48,49,
  //   a,b,c,d,e,f,80,81,3,4,5,6,7,48,49,4a,b,c,d,e,f,80,81,82,4,5,6,7,48,49,4a,4b,c,d,e,
  //   f,80,81,82,83,5,6,7,48,49,4a,4b,4c,d,e,f,80,81,82,83,84,6,7,48,49,4a,4b,4c,4d,e,f,
  //   80,81,82,83,84,85,7,48,49,4a,4b,4c,4d,4e,f,80,81,82,83,84,85,86,8,9,a,b,c,d,e,f,c0,
  //   c1,c2,c3,c4,c5,c6,c7,9,a,b,c,d,e,f,80,c1,c2,c3,c4,c5,c6,c7,88,a,b,c,d,e,f,80,81,c2,
  //   c3,c4,c5,c6,c7,88,89,b,c,d,e,f,80,81,82,c3,c4,c5,c6,c7,88,89,8a,c,d,e,f,80,81,82,
  //   83,c4,c5,c6,c7,88,89,8a,8b,d,e,f,80,81,82,83,84,c5,c6,c7,88,89,8a,8b,8c,e,f,80,81,
  //   82,83,84,85,c6,c7,88,89,8a,8b,8c,8d,f,80,81,82,83,84,85,86,c7,88,89,8a,8b,8c,8d,8e,
  //   0,1,2,3,4,5,6,7,8,9,a,b,c,d,e,f,1,2,3,4,5,6,7,48,9,a,b,c,d,e,f,80,2,3,4,5,6,7,48,
  //   49,a,b,c,d,e,f,80,81,3,4,5,6,7,48,49,4a,b,c,d,e,f,80,81,82,4,5,6,7,48,49,4a,4b,c,
  //   d,e,f,80,81,82,83,5,6,7,48,49,4a,4b,4c,d,e,f,80,81,82,83,84,6,7,48,49,4a,4b,4c,4d,
  //   e,f,80,81,82,83,84,85,7,48,49,4a,4b,4c,4d,4e,f,80,81,82,83,84,85,86,8,9,a,b,c,d,e,
  //   f,c0,c1,c2,c3,c4,c5,c6,c7,9,a,b,c,d,e,f,80,c1,c2,c3,c4,c5,c6,c7,88,a,b,c,d,e,f,80,
  //   81,c2,c3,c4,c5,c6,c7,88,89,b,c,d,e,f,80,81,82,c3,c4,c5,c6,c7,88,89,8a,c,d,e,f,80,
  //   81,82,83,c4,c5,c6,c7,88,89,8a,8b,d,e,f,80,81,82,83,84,c5,c6,c7,88,89,8a,8b,8c,e,f,
  //   80,81,82,83,84,85,c6,c7,88,89,8a,8b,8c,8d,f,80,81,82,83,84,85,86,c7,88,89,8a,8b,8c,
  //   8d,8e,0,1,2,3,4,5,6,7,8,9,a,b,c,d,e,f,8f,0,1,2,3,4,5,6,47,8,9,a,b,c,d,e,8e,8f,0,1,
  //   2,3,4,5,46,47,8,9,a,b,c,d,8d,8e,8f,0,1,2,3,4,45,46,47,8,9,a,b,c,8c,8d,8e,8f,0,1,2,
  //   3,44,45,46,47,8,9,a,b,8b,8c,8d,8e,8f,0,1,2,43,44,45,46,47,8,9,a,8a,8b,8c,8d,8e,8f,
  //   0,1,42,43,44,45,46,47,8,9,89,8a,8b,8c,8d,8e,8f,0,41,42,43,44,45,46,47,8,c8,c9,ca,
  //   cb,cc,cd,ce,cf,0,1,2,3,4,5,6,7,87,c8,c9,ca,cb,cc,cd,ce,8f,0,1,2,3,4,5,6,86,87,c8,
  //   c9,ca,cb,cc,cd,8e,8f,0,1,2,3,4,5,85,86,87,c8,c9,ca,cb,cc,8d,8e,8f,0,1,2,3,4,84,85,
  //   86,87,c8,c9,ca,cb,8c,8d,8e,8f,0,1,2,3,83,84,85,86,87,c8,c9,ca,8b,8c,8d,8e,8f,0,1,
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  //   contents of ALUDH (hex, n*v repeats v):
  //   0,1,2,3,4,5,6,7,8,9,a,b,c,d,e,f,1,1,3,3,5,5,7,7,9,9,b,b,d,d,f,f,2,3,2,3,6,7,6,7,a,
  //   b,a,b,e,f,e,f,3,3,3,3,7,7,7,7,b,b,b,b,f,f,f,f,4,5,6,7,4,5,6,7,c,d,e,f,c,d,e,f,5,5,
  //   7,7,5,5,7,7,d,d,f,f,d,d,f,f,6,7,6,7,6,7,6,7,e,f,e,f,e,f,e,f,7,7,7,7,7,7,7,7,f,f,f,
  //   f,f,f,f,f,8,9,a,b,c,d,e,f,8,9,a,b,c,d,e,f,9,9,b,b,d,d,f,f,9,9,b,b,d,d,f,f,a,b,a,b,
  //   e,f,e,f,a,b,a,b,e,f,e,f,b,b,b,b,f,f,f,f,b,b,b,b,f,f,f,f,c,d,e,f,c,d,e,f,c,d,e,f,c,
  //   d,e,f,d,d,f,f,d,d,f,f,d,d,f,f,d,d,f,f,e,f,e,f,e,f,e,f,e,f,e,f,e,f,e,f,f,f,f,f,f,f,
  //   f,f,f,f,f,f,f,f,f,f,0,0,0,0,0,0,0,0,0,0,0,0,0,0,0,0,0,1,0,1,0,1,0,1,0,1,0,1,0,1,0,
  //   1,0,0,2,2,0,0,2,2,0,0,2,2,0,0,2,2,0,1,2,3,0,1,2,3,0,1,2,3,0,1,2,3,0,0,0,0,4,4,4,4,
  //   0,0,0,0,4,4,4,4,0,1,0,1,4,5,4,5,0,1,0,1,4,5,4,5,0,0,2,2,4,4,6,6,0,0,2,2,4,4,6,6,0,
  //   1,2,3,4,5,6,7,0,1,2,3,4,5,6,7,0,0,0,0,0,0,0,0,8,8,8,8,8,8,8,8,0,1,0,1,0,1,0,1,8,9,
  //   8,9,8,9,8,9,0,0,2,2,0,0,2,2,8,8,a,a,8,8,a,a,0,1,2,3,0,1,2,3,8,9,a,b,8,9,a,b,0,0,0,
  //   0,4,4,4,4,8,8,8,8,c,c,c,c,0,1,0,1,4,5,4,5,8,9,8,9,c,d,c,d,0,0,2,2,4,4,6,6,8,8,a,a,
  //   c,c,e,e,0,1,2,3,4,5,6,7,8,9,a,b,c,d,e,f,0,1,2,3,4,5,6,7,8,9,a,b,c,d,e,f,1,0,3,2,5,
  //   4,7,6,9,8,b,a,d,c,f,e,2,3,0,1,6,7,4,5,a,b,8,9,e,f,c,d,3,2,1,0,7,6,5,4,b,a,9,8,f,e,
  //   d,c,4,5,6,7,0,1,2,3,c,d,e,f,8,9,a,b,5,4,7,6,1,0,3,2,d,c,f,e,9,8,b,a,6,7,4,5,2,3,0,
  //   1,e,f,c,d,a,b,8,9,7,6,5,4,3,2,1,0,f,e,d,c,b,a,9,8,8,9,a,b,c,d,e,f,0,1,2,3,4,5,6,7,
  //   9,8,b,a,d,c,f,e,1,0,3,2,5,4,7,6,a,b,8,9,e,f,c,d,2,3,0,1,6,7,4,5,b,a,9,8,f,e,d,c,3,
  //   2,1,0,7,6,5,4,c,d,e,f,8,9,a,b,4,5,6,7,0,1,2,3,d,c,f,e,9,8,b,a,5,4,7,6,1,0,3,2,e,f,
  //   c,d,a,b,8,9,6,7,4,5,2,3,0,1,f,e,d,c,b,a,9,8,7,6,5,4,3,2,1,0,0,0,0,0,0,0,0,0,0,0,0,
  //   0,0,0,0,0,1,1,1,1,1,1,1,1,1,1,1,1,1,1,1,1,2,2,2,2,2,2,2,2,2,2,2,2,2,2,2,2,3,3,3,3,
  //   3,3,3,3,3,3,3,3,3,3,3,3,4,4,4,4,4,4,4,4,4,4,4,4,4,4,4,4,5,5,5,5,5,5,5,5,5,5,5,5,5,
  //   5,5,5,6,6,6,6,6,6,6,6,6,6,6,6,6,6,6,6,7,7,7,7,7,7,7,7,7,7,7,7,7,7,7,7,8,8,8,8,8,8,
  //   8,8,8,8,8,8,8,8,8,8,9,9,9,9,9,9,9,9,9,9,9,9,9,9,9,9,a,a,a,a,a,a,a,a,a,a,a,a,a,a,a,
  //   a,b,b,b,b,b,b,b,b,b,b,b,b,b,b,b,b,c,c,c,c,c,c,c,c,c,c,c,c,c,c,c,c,d,d,d,d,d,d,d,d,
  //   d,d,d,d,d,d,d,d,e,e,e,e,e,e,e,e,e,e,e,e,e,e,e,e,f,f,f,f,f,f,f,f,f,f,f,f,f,f,f,f,0,
  //   1,2,3,4,5,6,7,8,9,a,b,c,d,e,f,1,2,3,4,5,6,7,8,9,a,b,c,d,e,f,0,2,3,4,5,6,7,8,9,a,b,
  //   c,d,e,f,0,1,3,4,5,6,7,8,9,a,b,c,d,e,f,0,1,2,4,5,6,7,8,9,a,b,c,d,e,f,0,1,2,3,5,6,7,
  //   8,9,a,b,c,d,e,f,0,1,2,3,4,6,7,8,9,a,b,c,d,e,f,0,1,2,3,4,5,7,8,9,a,b,c,d,e,f,0,1,2,
  //   3,4,5,6,8,9,a,b,c,d,e,f,0,1,2,3,4,5,6,7,9,a,b,c,d,e,f,0,1,2,3,4,5,6,7,8,a,b,c,d,e,
  //   f,0,1,2,3,4,5,6,7,8,9,b,c,d,e,f,0,1,2,3,4,5,6,7,8,9,a,c,d,e,f,0,1,2,3,4,5,6,7,8,9,
  //   a,b,d,e,f,0,1,2,3,4,5,6,7,8,9,a,b,c,e,f,0,1,2,3,4,5,6,7,8,9,a,b,c,d,f,0,1,2,3,4,5,
  //   6,7,8,9,a,b,c,d,e,0,1,2,3,4,5,6,7,8,9,a,b,c,d,e,f,1,2,3,4,5,6,7,8,9,a,b,c,d,e,f,0,
  //   2,3,4,5,6,7,8,9,a,b,c,d,e,f,0,1,3,4,5,6,7,8,9,a,b,c,d,e,f,0,1,2,4,5,6,7,8,9,a,b,c,
  //   d,e,f,0,1,2,3,5,6,7,8,9,a,b,c,d,e,f,0,1,2,3,4,6,7,8,9,a,b,c,d,e,f,0,1,2,3,4,5,7,8,
  //   9,a,b,c,d,e,f,0,1,2,3,4,5,6,8,9,a,b,c,d,e,f,0,1,2,3,4,5,6,7,9,a,b,c,d,e,f,0,1,2,3,
  //   4,5,6,7,8,a,b,c,d,e,f,0,1,2,3,4,5,6,7,8,9,b,c,d,e,f,0,1,2,3,4,5,6,7,8,9,a,c,d,e,f,
  //   0,1,2,3,4,5,6,7,8,9,a,b,d,e,f,0,1,2,3,4,5,6,7,8,9,a,b,c,e,f,0,1,2,3,4,5,6,7,8,9,a,
  //   b,c,d,f,0,1,2,3,4,5,6,7,8,9,a,b,c,d,e,0,1,2,3,4,5,6,7,8,9,a,b,c,d,e,f,f,0,1,2,3,4,
  //   5,6,7,8,9,a,b,c,d,e,e,f,0,1,2,3,4,5,6,7,8,9,a,b,c,d,d,e,f,0,1,2,3,4,5,6,7,8,9,a,b,
  //   c,c,d,e,f,0,1,2,3,4,5,6,7,8,9,a,b,b,c,d,e,f,0,1,2,3,4,5,6,7,8,9,a,a,b,c,d,e,f,0,1,
  //   2,3,4,5,6,7,8,9,9,a,b,c,d,e,f,0,1,2,3,4,5,6,7,8,8,9,a,b,c,d,e,f,0,1,2,3,4,5,6,7,7,
  //   8,9,a,b,c,d,e,f,0,1,2,3,4,5,6,6,7,8,9,a,b,c,d,e,f,0,1,2,3,4,5,5,6,7,8,9,a,b,c,d,e,
  //   f,0,1,2,3,4,4,5,6,7,8,9,a,b,c,d,e,f,0,1,2,3,3,4,5,6,7,8,9,a,b,c,d,e,f,0,1,2,2,3,4,
  //   5,6,7,8,9,a,b,c,d,e,f,0,1,1,2,3,4,5,6,7,8,9,a,b,c,d,e,f,0,0,1,2,3,4,5,6,7,8,f,0,1,
  //   2,3,4,5,6,7,8,9,a,b,c,d,e,f,0,1,2,3,4,5,0,1,2,3,4,5,6,7,8,f,0,1,2,3,4,5,6,7,8,9,a,
  //   b,c,d,e,f,0,1,2,3,4,5,0,1,2,3,4,5,6,7,8,f,0,1,2,3,4,5,6,7,8,9,a,b,c,d,e,f,0,1,2,3,
  //   4,5,0,1,2,3,4,5,6,7,8,f,0,1,2,3,4,5,6,7,8,9,a,b,c,d,e,f,0,1,2,3,4,5,0,1,2,3,4,5,6,
  //   7,8,f,0,1,2,3,4,5,6,7,8,9,a,b,c,d,e,f,0,1,2,3,4,5,0,1,2,3,4,5,6,7,8,f,0,1,2,3,4,5,
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endmodule
