// Digital circuit ASSERT.dig as structural Verilog
// This cricuit provide assert function. you can write value to 
// special address to excute assert function.
//  0xFD: value0,
//  0xFE: value1,
//  0xFF: function select(
//   1: assert v0 > v1, 
//   2: assert v0 = v1, 
//   3: assert v0 < v1)
// If assert  failed(F is high) when CLK falling edge, CLKO will output low.
module ASSERT (
  input  C,
  input  [7:0] A,
  input  [7:0] D,
  input  nWE,
  output Faf,
  output F_to
);

  wire and_1_out, and_2_out, and_3_out, and_4_out, comparator_1_eq, comparator_2_eq, comparator_3_eq,
       comparator_4_eq, comparator_4_gt, comparator_4_lt, comparator_5_eq, counter_1_ovf, not_1_out,
       not_2_out, not_3_out, not_4_out, rs_ff_1_q;
  wire [7:0] ARG, multiplexer_1_out, PAR0, PAR1;
  wire [15:0] counter_1_out;

  not not_1 (not_1_out, nWE);
  Comparator #(.Bits(8)) comparator_1 (.a(A), .b(8'hfd), .eq(comparator_1_eq));  // open: gt, lt
  Comparator #(.Bits(8)) comparator_2 (.a(A), .b(8'hfe), .eq(comparator_2_eq));  // open: gt, lt
  Comparator #(.Bits(8)) comparator_3 (.a(A), .b({8{1'b1}}), .eq(comparator_3_eq));  // open: gt, lt
  and and_1 (and_1_out, comparator_1_eq, not_1_out);
  and and_2 (and_2_out, comparator_2_eq, not_1_out);
  and and_3 (and_3_out, comparator_3_eq, not_1_out);
  Register #(.Bits(8)) ASTPAR0 (.D(D), .C(C), .en(and_1_out), .Q(PAR0));
  Register #(.Bits(8)) ASTPAR1 (.D(D), .C(C), .en(and_2_out), .Q(PAR1));
  Multiplexer #(.Bits(8)) multiplexer_1 (.sel(and_3_out), .in_0({8{1'b0}}), .in_1(D), .out(multiplexer_1_out));
  Comparator #(.Bits(8)) comparator_4 (
    .a(PAR0), .b(PAR1), .gt(comparator_4_gt), .eq(comparator_4_eq), .lt(comparator_4_lt));
  Register #(.Bits(8)) ASTARG (.D(multiplexer_1_out), .C(C), .en(1'b1), .Q(ARG));
  not not_2 (not_2_out, comparator_4_gt);
  not not_3 (not_3_out, comparator_4_eq);
  not not_4 (not_4_out, comparator_4_lt);
  Comparator #(.Bits(8)) comparator_5 (.a(ARG), .b(8'h5), .eq(comparator_5_eq));  // open: gt, lt
  Multiplexer #(.Selector_Bits(3)) multiplexer_2 (
    .sel(ARG[2:0]), .in_0(1'b0), .in_1(not_2_out), .in_2(not_3_out), .in_3(not_4_out), .in_4(1'b1),
    .in_5(1'b0), .in_6(1'b0), .in_7(1'b0), .out(Faf));
  Counter #(.Bits(16)) counter_1 (
    .en(and_4_out), .C(C), .clr(comparator_5_eq), .out(counter_1_out), .ovf(counter_1_ovf));
  RS_FF rs_ff_1 (.S(comparator_5_eq), .C(C), .R(1'b0), .Q(rs_ff_1_q));  // open: nQ
  Comparator #(.Bits(16)) comparator_6 (.a({PAR1, PAR0}), .b(counter_1_out), .eq(F_to));  // open: gt, lt
  // Probe on counter_1_out
  // Probe on counter_1_ovf
  and and_4 (and_4_out, rs_ff_1_q, ~F_to);  // And

  // Other names for the same wires on the sheet: CLK = C

  // Notes on the sheet:
  //   A: Address to locate register
  //   D: Data in
  //   Faf: Assert false flag.
  //   CLKO will be disabled at next cycle if it's high.
  //   nWE: Write enable
  //   F_to: timeout flag
endmodule

/* Test case:
C	~WE	A	D	F_to
C	0	0xFD	0x10	x
C	0	0xFE	0	x	
C	0	0xFF	5	x	
repeat(16) C  1 0	0	x
C	1	0	0	1
C	1	0	0	1

C	0	0xFD	0x10	x
C	0	0xFE	0x10	x	
C	0	0xFF	5	x	
repeat(0x1010) C  1 0	0	x
C	1	0	0	1
C	1	0	0	1
*/
