// Digital circuit BUS_TRAN.dig as structural Verilog
module BUS_TRAN (
  input  SFR_HIT,
  input  SSFR,
  input  RAM_WE,
  input  nRAM_OE,
  input  [7:0] ADDR,
  input  [7:0] BUS_A,
  input  [7:0] BUS_B
);

  wire multiplexer_1_out, nOE, or_1_out, or_2_out;
  wire [2:2] nand_1_out;

  nand nand_1 (nand_1_out[2], ADDR[7], SSFR);
  Multiplexer #(.Selector_Bits(3)) multiplexer_1 (
    .sel({nand_1_out[2], SFR_HIT, nRAM_OE}), .in_0(1'b1), .in_1(RAM_WE), .in_2(1'b0), .in_3(1'b0),
    .in_4(1'b0), .in_5(1'b0), .in_6(1'b0), .in_7(1'b0), .out(multiplexer_1_out));
  not not_1 (nOE, multiplexer_1_out);
  or or_1 (or_1_out, ~RAM_WE, nOE);  // Or
  or or_2 (or_2_out, RAM_WE, nOE);
  assign BUS_B = ~or_1_out ? BUS_A : 8'bz;  // DriverInvSel driverinvsel_1
  assign BUS_A = ~or_2_out ? BUS_B : 8'bz;  // DriverInvSel driverinvsel_2

  // Other names for the same wires on the sheet: AB_nBA = RAM_WE

  // Notes on the sheet:
  //   ADDR: default 128
endmodule
