// Digital circuit CLKSWH.dig as structural Verilog
// stop ouput clock if input S  is high. if go is 1, clock will ouput normally.
module CLKSWH (
  input  SW,
  input  MC,
  input  GC,
  output C,
  output AC
);

  wire and_1_out, and_2_out, and_3_out, comparator_1_eq, comparator_3_eq, not_1_out, register_1_q, SWCLK,
       SYNC_MC_q, SYNC_SW_q;
  wire [3:0] counter_1_out;

  Counter #(.Bits(4)) counter_1 (.en(1'b1), .C(GC), .clr(comparator_3_eq), .out(counter_1_out));  // open: ovf
  Register SYNC_SW (.D(SW), .C(SWCLK), .en(1'b1), .Q(SYNC_SW_q));
  Register SYNC_MC (.D(MC), .C(SWCLK), .en(1'b1), .Q(SYNC_MC_q));
  Comparator #(.Bits(4)) comparator_1 (.a(counter_1_out), .b(4'b0000), .eq(comparator_1_eq));  // open: gt, lt
  Comparator #(.Bits(4)) comparator_2 (.a(counter_1_out), .b(4'b0110), .eq(SWCLK));  // open: gt, lt
  Comparator #(.Bits(4)) comparator_3 (.a(counter_1_out), .b(4'b1011), .eq(comparator_3_eq));  // open: gt, lt
  Register register_1 (.D(SYNC_MC_q), .C(SWCLK), .en(1'b1), .Q(register_1_q));
  // Probe SWCLK on SWCLK
  not not_1 (not_1_out, register_1_q);
  and and_1 (and_1_out, SYNC_MC_q, not_1_out);
  and and_2 (and_2_out, comparator_1_eq, and_1_out);
  and and_3 (and_3_out, comparator_3_eq, and_1_out);
  Multiplexer multiplexer_1 (.sel(SYNC_SW_q), .in_0(comparator_1_eq), .in_1(and_2_out), .out(C));
  Multiplexer multiplexer_2 (.sel(SYNC_SW_q), .in_0(comparator_3_eq), .in_1(and_3_out), .out(AC));

  // Notes on the sheet:
  //   C: CPU main clock
  //   AC: async compoent clock, 
  //   It is a little earlier than the CPU main CLK,
  //    and the high level time is short.
  //   so you can use it to generate WE signal for async RAM chip.
  //   SW: switch of manual and crystal clock.
  //   set 1 to usign manual clock
  //   MC: manual clock
  //   GC: generator clock, the clock to generate all other clock.
  //   postive edge check
endmodule
