// Digital circuit CLRIRR.dig as structural Verilog
// PC external, for debug purpose, laod PC from RF to this register.
// select byte PCEL when RS is 8, select byte PCEH when RS is 9.
module CLRIRR (
  input  [7:0] D,
  input  IRR_CLR,
  output [7:0] Q
);

  wire decoder_1_out_0, decoder_1_out_1, decoder_1_out_2, decoder_1_out_3, decoder_1_out_4, decoder_1_out_5,
       decoder_1_out_6, decoder_1_out_7, or_1_out;
  wire [7:0] bitextender_1_out, not_1_out;

  Decoder #(.Selector_Bits(3)) decoder_1 (
    .sel(D[2:0]), .out_0(decoder_1_out_0), .out_1(decoder_1_out_1), .out_2(decoder_1_out_2),
    .out_3(decoder_1_out_3), .out_4(decoder_1_out_4), .out_5(decoder_1_out_5), .out_6(decoder_1_out_6),
    .out_7(decoder_1_out_7));
  or or_1 (or_1_out, D[7], ~IRR_CLR);  // Or
  not not_1 (not_1_out[0], decoder_1_out_0);
  not not_2 (not_1_out[1], decoder_1_out_1);
  not not_3 (not_1_out[2], decoder_1_out_2);
  not not_4 (not_1_out[3], decoder_1_out_3);
  not not_5 (not_1_out[4], decoder_1_out_4);
  not not_6 (not_1_out[5], decoder_1_out_5);
  not not_7 (not_1_out[6], decoder_1_out_6);
  not not_8 (not_1_out[7], decoder_1_out_7);
  BitExtender #(.inputBits(1), .outputBits(8)) bitextender_1 (.in(or_1_out), .out(bitextender_1_out));
  assign Q = not_1_out | bitextender_1_out;  // Or or_2, 8 bits wide

  // Notes on the sheet:
  //   IRR_CLR: clear accepted interrupt
  //   74xx138
endmodule
