// Digital circuit CORE.dig as structural Verilog
module CORE (
  input  clk,
  input  RST,
  input  CLR,
  input  in_4,
  input  [11:0] MIPCBI,
  input  [15:0] PCBIA1,
  input  MIPCBE,
  input  PCBE1,
  input  [15:0] PCBIA2,
  input  PCBE2
);

  wire ALUD_CO, and_2_out, and_3_out, and_4_out, ASSERT_p5, BR_CPLQ, BR_Q, button_1_out, CLK_t, CLKA, CLKR,
       comparator_1_eq, comparator_1_gt, comparator_1_lt, comparator_2_eq, comparator_3_eq, comparator_4_eq,
       decoder_1_out_0, decoder_1_out_1, decoder_1_out_2, decoder_1_out_3, decoder_1_out_4, decoder_1_out_5,
       decoder_1_out_6, decoder_1_out_7, dipswitch_1_out, DIRECT_OE, DIRECT_WE, DPC_JUMP, IRQ_CLR, IRQ_OE,
       nALUDH_OE, nALUDL_OE, nALUS_OE, nCLR, nDPC_JUMP, nIMMED_OE, not_8_out, not_13_out, nRAM_OE, nROM_OE,
       nSFR_OE, nXRAM_OE, or_1_out, RAM_OE, RAM_WE, RF_SFR, RF_WE, RFSRCR_WE, RI, SR_WE, TI, WR_WE, XRAM_WE;
  wire [2:0] BR_SRC, BUS_SRC, JUMP_TYPE;
  wire [3:0] ALUSD_FUNC, multiplexer_2_out, RF_SRC;
  wire [4:4] multiplexer_2_out_2;
  wire [5:0] nand_1_out;
  wire [7:0] BUS_D, DUMP_p5, IMMED, RF_Q;
  wire [7:4] RFSRCR_q;
  wire [11:0] ADDRESS, MIPC;
  wire [15:0] ADDR_16, PCER_q;
  wire [47:46] DECODER_2_d;

  SBUF sbuf_1 (.IO(BUS_D), .CLK(CLK_t), .A(ADDR_16[15:8]), .OE(DIRECT_OE), .WE(DIRECT_WE), .RI(RI), .TI(TI));
  Comparator #(.Bits(8)) comparator_1 (
    .a(RF_Q), .b(IMMED), .gt(comparator_1_gt), .eq(comparator_1_eq), .lt(comparator_1_lt));
  Decoder #(.Selector_Bits(3)) decoder_1 (
    .sel(BUS_SRC), .out_0(decoder_1_out_0), .out_1(decoder_1_out_1), .out_2(decoder_1_out_2),
    .out_3(decoder_1_out_3), .out_4(decoder_1_out_4), .out_5(decoder_1_out_5), .out_6(decoder_1_out_6),
    .out_7(decoder_1_out_7));
  not not_1 (nALUS_OE, decoder_1_out_0);
  not not_2 (nALUDL_OE, decoder_1_out_1);
  not not_3 (nALUDH_OE, decoder_1_out_2);
  not not_4 (nIMMED_OE, decoder_1_out_3);
  not not_5 (nRAM_OE, decoder_1_out_4);
  not not_6 (nXRAM_OE, decoder_1_out_5);
  not not_7 (nROM_OE, decoder_1_out_6);
  not not_8 (not_8_out, decoder_1_out_7);
  DCOUTER #(.generic("Bits := 12;")) dcouter_1 (
    .CLK(CLK_t), .CLR(nCLR), .CNT(1'b1), .LE(nDPC_JUMP), .D(ADDRESS), .Q(MIPC));
  Multiplexer #(.Selector_Bits(3)) multiplexer_1 (
    .sel(JUMP_TYPE), .in_0(1'b0), .in_1(1'b1), .in_2(comparator_1_gt), .in_3(comparator_1_eq),
    .in_4(comparator_1_lt), .in_5(BR_Q), .in_6(RST), .in_7(1'b0), .out(DPC_JUMP));
  not not_9 (IRQ_OE, not_8_out);
  assign BUS_D = ~nIMMED_OE ? IMMED : 8'bz;  // DriverInvSel driverinvsel_1
  PullDown #(.Bits(8)) pulldown_1 (.out(BUS_D));
  assign BUS_D = ~nSFR_OE ? RF_Q : 8'bz;  // DriverInvSel driverinvsel_2
  PCE PCER (.CLK(CLK_t), .D(BUS_D), .RS(RF_SRC), .WE(RF_WE), .Q(PCER_q));
  not not_10 (nDPC_JUMP, DPC_JUMP);
  not not_11 (RAM_OE, nRAM_OE);
  // Probe on BUS_D
  ROM #(.AddrBits(12), .Bits(48)) DECODER_2 (
    .A(MIPC), .sel(1'b1),
    .D({DECODER_2_d, IMMED, ADDRESS, JUMP_TYPE, IRQ_CLR, ALUSD_FUNC, XRAM_WE, RAM_WE, RFSRCR_WE, BR_CPLQ, BR_SRC, SR_WE, WR_WE, BUS_SRC, RF_SFR, RF_WE, RF_SRC}));
  Register #(.Bits(8)) RFSRCR (.D(BUS_D), .C(CLK_t), .en(RFSRCR_WE), .Q({RFSRCR_q, nand_1_out[3:0]}));
  and and_1 (nand_1_out[4], RFSRCR_q[4], RAM_WE);
  nand nand_1 (nand_1_out[5], RFSRCR_q[4], RAM_OE);
  Comparator #(.Bits(12)) comparator_2 (.a(MIPCBI), .b(MIPC), .eq(comparator_2_eq));  // open: gt, lt
  Comparator #(.Bits(16)) comparator_3 (.a(PCBIA1), .b(PCER_q), .eq(comparator_3_eq));  // open: gt, lt
  Comparator #(.Bits(16)) comparator_4 (.a(PCBIA2), .b(PCER_q), .eq(comparator_4_eq));  // open: gt, lt
  and and_2 (and_2_out, comparator_2_eq, MIPCBE);
  and and_3 (and_3_out, comparator_3_eq, PCBE1);
  and and_4 (and_4_out, comparator_4_eq, PCBE2);
  Multiplexer #(.Bits(6)) multiplexer_2 (
    .sel(RF_SFR), .in_0({1'b1, RF_WE, RF_SRC}), .in_1(nand_1_out),
    .out({nSFR_OE, multiplexer_2_out_2[4], multiplexer_2_out}));
  // Probe on MIPC
  // Probe on RF_SRC
  // Probe on RF_WE
  // Probe on RF_SFR
  // Probe on BUS_SRC
  // Probe on WR_WE
  // Probe on SR_WE
  // Probe on BR_SRC
  // Probe on BR_CPLQ
  // Probe on RFSRCR_WE
  // Probe on RAM_WE
  // Probe on XRAM_WE
  // Probe on ALUSD_FUNC
  // Probe on IRQ_CLR
  // Probe on JUMP_TYPE
  // Probe on ADDRESS
  // Probe on IMMED
  // EXTCTL EXT: pin names not known; wires that end beside it: DIRECT_WE, ADDR_16[15:8], BUS_D, CLK_t
  // ASSERT ASSERT: pin names not known; wires that end beside it: CLK_t, BUS_D, ADDR_16[15:8], DIRECT_WE, ASSERT_p5, CLK_t
  not not_12 (nCLR, CLR);
  DipSwitch dipswitch_1 (.out(dipswitch_1_out));
  CLKSWH clkswh_1 (.SW(dipswitch_1_out), .MC(button_1_out), .GC(clk), .C(CLKR), .AC(CLKA));
  Button button_1 (.out(button_1_out));
  // reg_file RF: pin names not known; wires that end beside it: CLK_t, multiplexer_2_out, BUS_D, multiplexer_2_out_2[4], multiplexer_2_out_2[4], RF_Q
  // Probe on RF_Q
  // DUMP DUMP: pin names not known; wires that end beside it: DIRECT_WE, ADDR_16[15:8], BUS_D, CLK_t, DUMP_p5
  or or_1 (or_1_out, ASSERT_p5, and_2_out, and_3_out, and_4_out);
  reg__sync_clear #(.generic("Bits := 8;")) WR (.D(BUS_D), .CLK(CLK_t), .CLR(CLR), .LE(WR_WE), .Q(ADDR_16[7:0]));
  reg__sync_clear #(.generic("Bits := 8;")) SR (.D(BUS_D), .CLK(CLK_t), .CLR(CLR), .LE(SR_WE), .Q(ADDR_16[15:8]));
  and and_5 (DIRECT_WE, RF_SFR, RAM_WE);
  and and_6 (DIRECT_OE, RF_SFR, RAM_OE);
  STALL STALL (.C(CLKR), .AC(or_1_out), .S(in_4), .OAC(CLK_t));  // open: G, nCLR, O
  INT INT (
    .CLK(CLK_t), .CLR(CLR), .A(ADDR_16[15:8]), .D(BUS_D), .WE(DIRECT_WE), .OE(DIRECT_OE), .nIRQ_OE(IRQ_OE),
    .CAI(IRQ_CLR), .RI(RI), .TI(TI), .IRQ(DUMP_p5));
  // Probe on ADDR_16[7:0]
  // Probe on ADDR_16[15:8]
  // Probe on DUMP_p5
  not not_13 (not_13_out, nROM_OE);
  ALU ALU (
    .A(RF_Q), .B(ADDR_16[7:0]), .S(ALUSD_FUNC), .CI(BR_Q), .SOE(nALUS_OE), .DOE(nALUDL_OE), .FOE(nALUDH_OE),
    .O(BUS_D), .ALUDF(ALUD_CO));
  ROM #(.AddrBits(16), .Bits(8)) ROM (.A(ADDR_16), .sel(not_13_out), .D(BUS_D));
  RAM RAM (.AC(CLKA), .A(ADDR_16[15:8]), .WE(RAM_WE), .nOE(nRAM_OE), .Dt(RF_SFR), .O(BUS_D));
  XRAM XRAM (.CLKA(CLK_t), .A(ADDR_16), .WE(XRAM_WE), .nOE(nXRAM_OE), .O(BUS_D));
  BR BR (
    .CLK(CLK_t), .nCLR(nCLR), .S(BR_SRC), .I4(ALUD_CO), .I5(ALUD_CO), .I7(RF_Q[0]), .I6(RF_Q[7]),
    .CPQ(BR_CPLQ), .Q(BR_Q));

  // Other names for the same wires on the sheet: ADDR_RAM[7:0] = ADDR_16[15:8]; GO = in_4

  // Notes on the sheet:
  //   clk: Hz: 2147483647
  //   LS137/LS138
  //   LS161
  //   LS151/LS251
  //   contents of DECODER_2 (hex, n*v repeats v):
  //   ea7100248,100449,19a,102886,381855,3c2a58,3c0459,20084200100a,3002be00000a,38010e00000a,
  //   3c009e00000a,3e003e00000a,100245,34044a,e68910046,3d007600000a,3d805600000a,100245,
  //   14044a,500,e68910046,3d407200000a,59c,c800c,100246,311860,3c2858,e68bc0059,e68b80096,
  //   3c808e00000a,100245,14044a,300,4c0,e68920046,3c0e3900000a,100241,100442,e68920046,
  //   3a00ae00000a,100245,34044a,e68800116,3900e600000a,3980c600000a,100245,14044a,500,
  //   e68800116,3940e200000a,59c,c800c,320,301856,3c2858,e68bc0059,e688000d6,3880fe00000a,
  //   100245,14044a,300,4c0,e68800156,380e2500000a,100241,100442,e68800156,34020200000a,
  //   36014200000a,19c,100245,34044a,11d,25001d,4e6200180d,101a4c,82858,3c1059,32cc,e688c0059,
  //   3501a600000a,35816a00000a,100245,14044a,500,11c,100246,1d004c,10024c,e689c0056,35419200000a,
  //   59c,c800c,320,30005d,24021d,310060,4e5a001acd,3c2a58,82cbc0459,205,42856,1a2801800,
  //   e68800000,e68b00015,3481da00000a,34c1b200000a,e68b04015,39c,30005d,2c001d,28041c,
  //   c800c,1b20,18024d,311860,3c2858,e68bc0059,340e3900000a,19c,100440,300,10044c,c800c,
  //   310060,241810,3c2858,e68bc0059,32021a00000a,100245,34044a,300,110046,e68b00056,31026a00000a,
  //   31823a00000a,100245,14044a,500,100246,116,e68b10040,31426600000a,59c,c800c,320,30005c,
  //   100246,310060,10024c,301856,3c2858,e68bc0059,e68bc0016,30829e00000a,30c27600000a,
  //   e68b00015,39c,30005d,2c001d,28041c,c800c,1320,18024d,311860,3c2858,e68bc0059,300e2500000a,
  //   59c,c800c,320,200410,311840,3c2858,e68bc0059,28059600000a,2c03d200000a,2e02f200000a,
  //   19d,100245,34044a,11c,10124d,c2a5c,302815,4e5a801ac0,3c2a58,82cbc0459,2d036200000a,
  //   2d832600000a,19d,100245,14044a,500,11c,10124d,c2a5c,302815,4e5a801ac0,3c2a58,82cbc0459,
  //   2d434a00000a,59c,c800c,1320,c2a46,302815,4e5a801ac0,3c2a58,82cbc0459,1380,c2a46,302815,
  //   4e5a801ac0,3c2a58,82cbc0459,2c839e00000a,2cc37200000a,382885,e68b00015,39c,30005d,
  //   2c001d,28041c,c800c,320,1c288d,18424d,311860,3c2858,e68bc0059,2c0e3900000a,39c,30005d,
  //   2c001d,28041c,c800c,320,1c009d,38028d,342885,301815,3c2858,e68bc0059,2a03fa00000a,
  //   59c,c800c,320,30005c,100245,34044a,11184c,3c2858,e68bc0059,29052a00000a,29842a00000a,
  //   59c,c800c,320,30005c,100245,14044a,500,11184c,3c2858,e68bc0059,29442e00000a,10dc,
  //   44d2183816,81207,8285c,18381c,18101d,44de183816,81207,8285c,18381c,18101d,44e6183816,
  //   81207,8285c,18381c,18101d,44ee183816,81207,8285c,18381c,18101d,44f6183816,81207,8285c,
  //   18381c,18101d,44fe183816,81207,8285c,18381c,18101d,4506183816,81207,8285c,18381c,
  //   18101d,450e183816,81207,8285c,183a1c,51498101d,d6,10d7,e68ac0055,18381c,18101d,18381c,
  //   18101d,18381c,18101d,18381c,18101d,18381c,18101d,18381c,18101d,183a1c,18101d,300057,
  //   242887,100a4d,300056,e68ac0055,28856200000a,28c53a00000a,3c6851,e68bc0052,39c,30005d,
  //   2c001d,28041c,c800c,320,1c288d,301815,3c2858,e68bc0059,280e2500000a,39c,30005d,2c001d,
  //   28041c,c800c,320,1c009d,38028d,142885,301815,3c2858,e68bc0059,24069a00000a,2605c200000a,
  //   103245,34044a,31d,c0286,30005c,20c,240055,10024d,e688c0056,25064200000a,2585f200000a,
  //   103245,14044a,500,31d,c0286,30005c,20c,240055,10024d,e688c0056,25462200000a,3005,
  //   59c,c800c,320,30005d,c0286,30005c,20c,240055,10024d,e608c1856,3005,39d,c0286,30005c,
  //   20c,240055,10024d,e608c1856,24868600000a,24c65a00000a,101246,82a41,3c0442,e68800196,
  //   3005,39c,30005d,2c001d,28041c,c800c,320,18024d,311860,3c2858,e68bc0059,240e3900000a,
  //   1992,3c2a58,3c0459,e60801991,2206ba00000a,19c,100245,34044a,300,c800c,10044c,e60b11860,
  //   2107e600000a,2186ea00000a,19c,100245,14044a,500,300,c800c,10044c,311860,3c2858,e68bc0059,
  //   21471600000a,59c,c800c,320,30185d,3c2a58,3c0459,59c,10024d,c800c,e60b11860,dc,47e2101247,
  //   47da1c3016,1c101c,c284c,732801000,c185c,1c3016,1c101c,c284c,746801000,c185c,1c3016,
  //   1c101c,c284c,75a801000,c185c,1c3016,1c101c,c284c,76e801000,c185c,1c3016,1c101c,c284c,
  //   782801000,c185c,1c3016,1c101c,c284c,796801000,c185c,1c3016,1c101c,c284c,7aa801000,
  //   c185c,1c3016,1c101c,c284c,7ca801000,c1a5c,300057,1c1016,e68ac0055,10024c,300057,1c1016,
  //   e68ac0055,10d7,e68ac0055,e68ac4055,20882a00000a,20c7fe00000a,101246,82a48,3c0449,
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  //   at28c64
  //   core is at28c64
  //   contents of ROM (hex, n*v repeats v):
  //   2,c,3d,2,e,5a,30,99,fd,c2,99,8f,99,22,0,0,0,0,0,2,d,e7,2,3,27,e8,64,80,f8,e9,33,e8,
  //   33,60,11,4,60,f0,ed,33,ec,33,70,9,e8,fc,e9,fd,ea,fe,eb,ff,22,4,60,de,d3,eb,9f,ea,
  //   9e,e9,9d,e8,c2,e7,8c,f0,c2,f7,95,f0,40,c,e8,cc,f8,e9,cd,f9,ea,ce,fa,eb,cf,fb,12,2,
  //   f2,85,d0,f0,58,4,70,3,20,d5,b3,e8,4,70,7,50,2,b2,d5,2,3,31,92,d5,ec,4,60,f7,e4,cc,
  //   c0,e0,c3,98,f8,60,3b,94,18,60,8,40,d,d0,e0,fb,2,3,9,e4,fb,fa,c9,fc,80,28,e8,30,e4,
  //   6,e4,c9,fb,e4,ca,fc,e8,30,e3,5,e4,c9,ca,cb,fc,e8,54,7,60,10,f8,c3,e9,13,f9,ea,13,
  //   fa,eb,13,fb,ec,13,fc,d8,f1,30,f5,2f,c3,e4,9c,fc,ef,9b,ff,ee,9a,fe,ed,99,fd,d0,e0,
  //   fb,ef,4e,4d,4c,70,12,22,db,3,2,3,2e,ec,2c,fc,ef,33,ff,ee,33,fe,ed,33,fd,ed,30,e7,
  //   eb,2,3,9,ef,2b,ff,ee,3a,fe,ed,39,fd,d0,e0,fb,50,13,b,bb,0,3,2,3,31,ed,13,fd,ee,13,
  //   fe,ef,13,ff,ec,13,fc,2,3,9,ec,4d,60,11,e8,49,70,17,ed,33,ec,33,4,60,d,e4,fc,ff,fe,
  //   fd,22,e9,33,e8,33,4,70,f8,2,3,27,12,2,f2,58,4,60,9,e4,cc,24,81,50,6,28,50,9,2,3,31,
  //   28,40,3,2,3,2e,c0,e0,eb,4a,70,44,b9,80,6,d0,e0,fb,2,3,1d,ef,4e,70,1c,bd,80,8,eb,ff,
  //   ea,fe,e9,fd,80,eb,e9,8d,f0,a4,fe,e5,f0,2,1,f7,e9,cd,f9,ea,fe,eb,ff,ef,89,f0,a4,fc,
  //   e5,f0,ce,89,f0,a4,2e,ff,e4,35,f0,cd,89,f0,a4,2d,fe,e4,35,f0,80,67,ef,4e,70,5,bd,80,
  //   d7,80,c3,ef,8b,f0,a4,ac,f0,ee,8b,f0,a4,2c,fc,e4,35,f0,f8,ef,8a,f0,a4,2c,e5,f0,38,
  //   fc,e4,33,cb,8d,f0,a4,2c,fc,e5,f0,3b,f8,ee,8a,f0,a4,2c,fc,e5,f0,38,f8,e4,33,cf,89,
  //   f0,a4,2c,fc,e5,f0,38,cf,34,0,ce,89,f0,a4,2f,ff,e5,f0,3e,fe,e4,33,c9,8d,f0,a4,2e,fe,
  //   e5,f0,39,cd,8a,f0,a4,2f,ff,e5,f0,3e,fe,e4,3d,fd,33,d0,e0,fb,50,7,b,bb,0,f,2,3,31,
  //   ec,2c,fc,ef,33,ff,ee,33,fe,ed,33,fd,2,3,9,2,3,31,ec,5d,4,60,5,e8,59,4,70,3,2,3,27,
  //   12,2,f2,58,4,60,f6,ec,48,60,f2,ec,70,4,fd,fe,ff,22,c8,60,db,24,81,c8,50,9,c3,98,60,
  //   2,50,6,2,3,2e,98,50,ca,f5,82,e9,29,4b,4a,70,5,ab,82,2,3,1d,75,f0,0,7c,1a,78,80,c3,
  //   ef,9b,ee,9a,ed,99,40,d,c3,ef,9b,ff,ee,9a,fe,ed,99,fd,e8,42,f0,dc,23,ac,f0,d0,e0,ff,
  //   d0,e0,fe,d0,e0,fd,ab,82,20,e7,10,1b,eb,60,ba,ec,2c,fc,ef,33,ff,ee,33,fe,ed,33,fd,
  //   2,3,9,e8,3,f8,30,e7,5,c0,f0,75,f0,0,ef,2f,ff,ee,33,fe,ed,33,fd,40,b8,30,e7,c2,80,
  //   aa,75,f0,20,80,e,75,f0,10,80,5,75,f0,8,7d,0,7e,0,7f,0,33,92,d5,30,d5,3,12,6,21,ec,
  //   33,40,10,ef,33,ff,ee,33,fe,ed,33,fd,ec,33,fc,d5,f0,ed,22,e5,f0,24,7e,a2,d5,13,cc,
  //   92,e7,cd,ce,ff,22,e9,d2,e7,c9,33,e8,33,f8,92,d5,ed,d2,e7,cd,33,ec,33,fc,50,2,b2,d5,
  //   22,ec,30,e7,10,f,bf,0,c,e,be,0,8,d,bd,0,4,b,eb,60,14,a2,d5,eb,13,fc,ed,92,e7,fd,22,
  //   74,ff,fc,fd,fe,ff,22,e4,80,f8,a2,d5,74,ff,13,fc,7d,80,e4,80,ef,f9,20,e7,28,24,f9,
  //   50,3,79,7,e4,f4,24,2,fb,18,db,fd,e6,24,fb,50,14,e9,60,d,e4,f6,18,e6,4,f6,b4,a,8,e4,
  //   f6,d9,f5,74,1,f6,a,22,c2,d5,22,ed,33,ec,33,92,d5,fa,60,2a,b4,ff,33,ed,c2,e7,7b,ff,
  //   60,6,7a,3,79,90,e4,22,7a,3,79,99,20,d5,4,7a,3,79,94,22,4e,61,4e,0,2b,49,4e,46,0,2d,
  //   49,4e,46,0,e4,7a,8,f6,8,da,fc,7b,0,74,7,22,e8,c0,e0,ec,c0,e0,ed,c0,e0,ee,c0,e0,ef,
  //   c0,e0,ea,75,f0,10,a4,ca,ab,f0,75,f0,4d,a4,2b,fb,e4,35,f0,fc,ea,24,10,fa,eb,34,c5,
  //   fb,ec,34,d9,fc,ed,c2,e7,ff,75,f0,56,a4,f4,24,11,c5,f0,f4,34,c5,8f,f0,a4,2a,e5,f0,
  //   3b,e4,3c,f6,20,e7,14,12,4,9e,d0,e0,ff,d0,e0,fe,d0,e0,fd,d0,e0,fc,12,2,17,80,14,f4,
  //   4,12,4,9e,d0,e0,ff,d0,e0,fe,d0,e0,fd,d0,e0,fc,12,1,e,d0,e0,f8,e6,fa,ed,d2,e7,cd,33,
  //   ec,33,24,82,fb,e4,c3,cf,33,cf,ce,33,ce,cd,33,cd,33,db,f3,7b,7,75,f0,a,84,60,4,f6,
  //   8,1b,a,e5,f0,f6,8,8f,f0,74,a,a4,ff,ac,f0,8e,f0,74,a,a4,2c,fe,ac,f0,50,1,c,8d,f0,74,
  //   a,a4,2c,fd,e4,35,f0,f6,8,db,de,74,7,22,3f,80,0,0,41,20,0,0,42,c8,0,0,44,7a,0,0,46,
  //   1c,40,0,47,c3,50,0,49,74,24,0,4b,18,96,80,4c,be,bc,20,5a,e,1b,ca,67,53,c2,1c,74,9d,
  //   c5,ae,fb,60,6,54,7,60,1c,23,23,12,4,cc,eb,54,38,60,9,12,4,b8,12,4,c7,12,1,e,ec,f8,
  //   ed,f9,ee,fa,ef,cb,22,eb,12,4,c7,80,f1,54,38,3,24,1c,90,4,6e,fe,93,fc,e,ee,93,fd,e,
  //   ee,93,e,ce,93,ff,22,bb,1,6,89,82,8a,83,e0,22,50,2,e7,22,bb,fe,2,e3,22,89,82,8a,83,
  //   e4,93,22,bb,1,c,e5,82,29,f5,82,e5,83,3a,f5,83,e0,22,50,6,e9,25,82,f8,e6,22,bb,fe,
  //   6,e9,25,82,f8,e2,22,e5,82,29,f5,82,e5,83,3a,f5,83,e4,93,22,bb,1,6,89,82,8a,83,f0,
  //   22,50,2,f7,22,bb,fe,1,f3,22,ef,8d,f0,a4,a8,f0,cf,8c,f0,a4,28,ce,8d,f0,a4,2e,fe,22,
  //   bc,0,b,be,0,29,ef,8d,f0,84,ff,ad,f0,22,e4,cc,f8,75,f0,8,ef,2f,ff,ee,33,fe,ec,33,fc,
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  //   core is 6116
  //   L74+LS252
endmodule
