// Digital circuit DCOUTER.dig as structural Verilog
module DCOUTER (
  input  CLK,
  input  CLR,
  input  CNT,
  input  LE,
  input  [11:0] D,
  output [11:0] Q
);

  wire or_1_out;
  wire [3:0] multiplexer_1_out, multiplexer_1_out_2, multiplexer_1_out_3;
  wire [11:0] add_1_s;

  or or_1 (or_1_out, CNT, LE);
  reg4clr reg4clr_1 (.D(multiplexer_1_out), .CLK(CLK), .CLR(CLR), .LE(or_1_out), .Q(Q[3:0]));
  reg4clr reg4clr_2 (.D(multiplexer_1_out_2), .CLK(CLK), .CLR(CLR), .LE(or_1_out), .Q(Q[7:4]));
  reg4clr reg4clr_3 (.D(multiplexer_1_out_3), .CLK(CLK), .CLR(CLR), .LE(or_1_out), .Q(Q[11:8]));
  Multiplexer #(.Bits(12)) multiplexer_1 (
    .sel(LE), .in_0(add_1_s), .in_1(D), .out({multiplexer_1_out_3, multiplexer_1_out_2, multiplexer_1_out}));
  Add #(.Bits(12)) add_1 (.a(12'h1), .b(Q), .c_i(1'b0), .s(add_1_s));  // open: c_o

  // Notes on the sheet:
  //   CNT: Q = Q + 1, lower priority than LE
  //   LE: load value from D
endmodule
