// Digital circuit DUMP.dig as structural Verilog
// The circuit was using to make condition exit in Java
// (see Digitalc.exe's source code, MainCmd.java). 
// when you write a value greater than 0 to EXR, MainCmd.java will
// stop run and using ECR's value as exit code.
module DUMP (
  input  C,
  input  [7:0] A,
  input  [7:0] D,
  input  nWE,
  output [7:0] V0
);

  wire and_1_out, comparator_1_eq;

  Comparator #(.Bits(8)) comparator_1 (.a(A), .b(8'hfb), .eq(comparator_1_eq));  // open: gt, lt
  and and_1 (and_1_out, comparator_1_eq, ~nWE);  // And
  Register #(.Bits(8)) DUMPR (.D(D), .C(C), .en(and_1_out), .Q(V0));
  // Pins of 1 and 8 bits meet at D
  // Pins of 1 and 8 bits meet at V0
  // Pins of 1 and 8 bits meet at A

  // Notes on the sheet:
  //   C: CLK
  //   A: Address
  //   D: Data
  //   nWE: write enable
  //   V0: EXR value
endmodule
