// Digital circuit EXTCTL.dig as structural Verilog
// The circuit was using to make condition exit in Java
// (see Digitalc.exe's source code, MainCmd.java). 
// when you write a value greater than 0 to EXR, MainCmd.java will
// stop run and using ECR's value as exit code.
module EXTCTL (
  input  WE,
  input  [7:0] A,
  input  [7:0] D,
  input  C,
  output [7:0] V0,
  output [7:0] V1
);

  wire and_1_out, and_2_out, comparator_1_eq, comparator_2_eq;

  Comparator #(.Bits(8)) comparator_1 (.a(A), .b(8'hee), .eq(comparator_1_eq));  // open: gt, lt
  Comparator #(.Bits(8)) comparator_2 (.a(A), .b(8'hef), .eq(comparator_2_eq));  // open: gt, lt
  and and_1 (and_1_out, comparator_1_eq, WE);
  and and_2 (and_2_out, comparator_2_eq, WE);
  Register #(.Bits(8)) EXR (.D(D), .C(C), .en(and_1_out), .Q(V0));
  Register #(.Bits(8)) ECR (.D(D), .C(C), .en(and_2_out), .Q(V1));
  // Pins of 1 and 8 bits meet at D
  // Pins of 1 and 8 bits meet at V1
  // Pins of 1 and 8 bits meet at A
  // Pins of 1 and 8 bits meet at V0

  // Notes on the sheet:
  //   WE: write enable
  //   A: Address
  //   D: Data
  //   C: CLK
  //   V0: EXR value
  //   V1: ECR value
endmodule
