// Digital circuit INT_REG.dig as structural Verilog
// PC external, for debug purpose, laod PC from RF to this register.
// select byte PCEL when RS is 8, select byte PCEH when RS is 9.
module INT_REG (
  input  CLR,
  input  nWE,
  input  CII,
  input  [7:0] II,
  input  [7:0] D,
  input  C,
  output [7:0] Q
);

  wire [7:0] and_1_out, bitextender_1_out, multiplexer_1_out, nand_1_out;

  BitExtender #(.inputBits(1), .outputBits(8), .generic("this.outputBits = int(args.Bits);")) bitextender_1 (
    .in(CII), .out(bitextender_1_out));
  Multiplexer #(.Bits(8), .generic("this.Bits = int(args.Bits);")) multiplexer_1 (
    .sel(nWE), .in_0(D), .in_1(Q), .out(multiplexer_1_out));
  assign nand_1_out = ~(II & bitextender_1_out);  // NAnd nand_1, 8 bits wide
  assign and_1_out = multiplexer_1_out & nand_1_out;  // And and_1, 8 bits wide
  reg__sync_clear #(.generic("Bits := int(args.Bits);")) reg__sync_clear_1 (
    .D(and_1_out), .CLK(C), .CLR(CLR), .LE(1'b0), .Q(Q));

  // Notes on the sheet:
  //   C: Clock
endmodule
