// Digital circuit INT_TCON.dig as structural Verilog
// PC external, for debug purpose, laod PC from RF to this register.
// select byte PCEL when RS is 8, select byte PCEH when RS is 9.
module INT_TCON (
  input  [7:0] D,
  input  nWE,
  input  CII,
  input  CLK,
  input  CLR,
  output [3:0] IRQ,
  output [7:0] Q
);

  // INT_REG #(.generic("Bits := 4;")) int_reg_1: pin names not known; wires that end beside it: CLR, nWE, CII, {D[3], D[1], D[2], D[0]}, {D[7], D[5], D[3], D[1]}, CLK, {IRQ[3], IRQ[1], IRQ[2], IRQ[0]}
  // reg__sync_clear #(.generic("Bits := 4;")) reg__sync_clear_1: pin names not known; wires that end beside it: {D[6], D[4], D[2], D[0]}, CLK, CLR, nWE, {Q[6], Q[4], Q[2], Q[0]}

  assign {Q[7], Q[5], Q[3], Q[1]} = {IRQ[3], IRQ[1], IRQ[2], IRQ[0]};
endmodule
