// Digital circuit PER_INT_IO.dig as structural Verilog
// interrupt, IO:
// UART: SBUF, SCON
// external int: TCON
module PER_INT_IO (
  input  CLK,
  input  nRST,
  input  [7:0] A,
  input  [7:0] D,
  input  nWE,
  input  nOE,
  input  [7:0] nIRR_CLRB,
  input  nXINT0,
  input  nXINT1,
  output [7:0] IRR_Q
);

  wire CNTEN0, CNTEN1, CT0, CT1, d_ff_1_q, d_ff_2_q, d_ff_3_q, d_ff_4_q, G0, G1, IE0, IE1, IT0, IT1,
       not_1_out, not_2_out, nTR0, nTR1, sfr_ctl_1_nwe, sfr_ctl_2_nwe, sfr_ctl_3_nwe, sfr_ctl_4_nwe,
       sfr_ctl_5_noe, sfr_ctl_5_nwe, sfr_ctl_6_noe, sfr_ctl_6_nwe, sfr_ctl_7_noe, sfr_ctl_7_nwe,
       sfr_ctl_8_noe, sfr_ctl_8_nwe, T0OV, T1OV, TR0, TR1;
  wire [1:0] sfr_sbuf_1_ri;
  wire [5:0] TMOD_q;
  wire [7:1] sfr_tcon_1_q;
  wire [7:6] INTTIMERLUT_out;
  wire [15:0] sfr_timmer_1_q, sfr_timmer_2_q;

  not not_1 (not_1_out, nXINT0);
  not not_2 (not_2_out, nXINT1);
  D_FF d_ff_1 (.D(d_ff_2_q), .C(CLK), .Q(d_ff_1_q));  // open: nQ
  D_FF d_ff_2 (.D(not_1_out), .C(CLK), .Q(d_ff_2_q));  // open: nQ
  D_FF d_ff_3 (.D(d_ff_4_q), .C(CLK), .Q(d_ff_3_q));  // open: nQ
  D_FF d_ff_4 (.D(not_2_out), .C(CLK), .Q(d_ff_4_q));  // open: nQ
  LookUpTable #(.Bits(8)) INTTIMERLUT (
    .in0(d_ff_1_q), .in1(d_ff_2_q), .in2(d_ff_3_q), .in3(d_ff_4_q), .in4(IT0), .in5(IT1), .in6(TR0),
    .in7(TR1), .in8(G0), .in9(CT0), .in10(G1), .in11(CT1), .in12(1'b0),
    .out({INTTIMERLUT_out, nTR1, nTR0, CNTEN1, CNTEN0, IE1, IE0}));
  SFR_CTL sfr_ctl_1 (.nSFR_WE(nWE), .nSFR_OE(nOE), .A(A), .MADDR(8'h8a), .nWE(sfr_ctl_1_nwe));  // open: nOE
  SFR_CTL sfr_ctl_2 (.nSFR_WE(nWE), .nSFR_OE(nOE), .A(A), .MADDR(8'h8c), .nWE(sfr_ctl_2_nwe));  // open: nOE
  SFR_CTL sfr_ctl_3 (.nSFR_WE(nWE), .nSFR_OE(nOE), .A(A), .MADDR(8'h8b), .nWE(sfr_ctl_3_nwe));  // open: nOE
  SFR_CTL sfr_ctl_4 (.nSFR_WE(nWE), .nSFR_OE(nOE), .A(A), .MADDR(8'h8d), .nWE(sfr_ctl_4_nwe));  // open: nOE
  SFR_CTL sfr_ctl_5 (.nSFR_WE(nWE), .nSFR_OE(nOE), .A(A), .MADDR(8'h89), .nWE(sfr_ctl_5_nwe), .nOE(sfr_ctl_5_noe));
  SFR_TIMMER sfr_timmer_1 (
    .C(CLK), .nR(nRST), .D(D), .rld(nTR0), .nWEL(sfr_ctl_1_nwe), .nWEH(sfr_ctl_2_nwe), .en(CNTEN0),
    .ovf(T0OV), .Q(sfr_timmer_1_q));
  SFR_TIMMER sfr_timmer_2 (
    .C(CLK), .nR(nRST), .D(D), .rld(nTR1), .nWEL(sfr_ctl_3_nwe), .nWEH(sfr_ctl_4_nwe), .en(CNTEN1),
    .ovf(T1OV), .Q(sfr_timmer_2_q));
  reg__sync_clear #(.generic("Bits := 8;")) TMOD (
    .D(D), .CLK(CLK), .CLR(nRST), .LE(sfr_ctl_5_nwe), .Q({G1, CT1, TMOD_q[5:4], G0, CT0, TMOD_q[1:0]}));
  // Probe T0Q on sfr_timmer_1_q
  // Probe T1Q on sfr_timmer_2_q
  assign D = ~sfr_ctl_5_noe ? {G1, CT1, TMOD_q[5:4], G0, CT0, TMOD_q[1:0]} : 8'bz;  // DriverInvSel driverinvsel_1
  SFR_CTL sfr_ctl_6 (.nSFR_WE(nWE), .nSFR_OE(nOE), .A(A), .MADDR(8'h88), .nWE(sfr_ctl_6_nwe), .nOE(sfr_ctl_6_noe));
  SFR_CTL sfr_ctl_7 (.nSFR_WE(nWE), .nSFR_OE(nOE), .A(A), .MADDR(8'h98), .nWE(sfr_ctl_7_nwe), .nOE(sfr_ctl_7_noe));
  SFR_CTL sfr_ctl_8 (.nSFR_WE(nWE), .nSFR_OE(nOE), .A(A), .MADDR(8'h99), .nWE(sfr_ctl_8_nwe), .nOE(sfr_ctl_8_noe));
  SFR_TCON sfr_tcon_1 (
    .CLK(CLK), .nRST(nRST), .D(D), .nWE(sfr_ctl_6_nwe), .nOE(sfr_ctl_6_noe), .IRQ({T1OV, IE1, T0OV, IE0}),
    .nIRR_CB(nIRR_CLRB[3:0]),
    .Q({sfr_tcon_1_q[7], TR1, sfr_tcon_1_q[5], TR0, sfr_tcon_1_q[3], IT1, sfr_tcon_1_q[1], IT0}),
    .IRRQ(IRR_Q[3:0]));
  SFR_SCON sfr_scon_1 (
    .CLK(CLK), .nRST(nRST), .D(D), .nWE(sfr_ctl_7_nwe), .nOE(sfr_ctl_7_noe), .IRQ(sfr_sbuf_1_ri),
    .IRRQ(IRR_Q[4]));  // open: Q
  SFR_SBUF sfr_sbuf_1 (
    .CLK(CLK), .D(D), .nWE(sfr_ctl_8_nwe), .nOE(sfr_ctl_8_noe), .RI(sfr_sbuf_1_ri[0]), .TI(sfr_sbuf_1_ri[1]));

  assign IRR_Q[7:5] = 3'b000;

  // Other names for the same wires on the sheet: ADDR_SFR[7:0] = A; BUS_D[7:0] = D; nSFR_OE = nOE; nSFR_WE = nWE

  // Notes on the sheet:
  //   CLK: Hz: 2147483647
  //   A: address input
  //   D: Data Bus
  //   nWE: write enable
  //   The SFR in the corresponding address will read the data from  the data bus.
  //   nOE: output enable.
  //   The SFR in the corresponding address will drive the data  bus.
  //   contents of INTTIMERLUT (hex, n*v repeats v):
  //   30,30,31,31,30,30,31,31,32,32,33,33,32,32,33,33,30,30,31,30,30,30,31,30,32,32,33,
  //   32,32,32,33,32,30,30,31,31,30,30,31,31,32,32,33,33,30,30,31,31,30,30,31,30,30,30,
  //   31,30,32,32,33,32,30,30,31,30,24,24,25,25,24,24,25,25,26,26,27,27,26,26,27,27,24,
  //   24,25,24,24,24,25,24,26,26,27,26,26,26,27,26,24,24,25,25,24,24,25,25,26,26,27,27,
  //   24,24,25,25,24,24,25,24,24,24,25,24,26,26,27,26,24,24,25,24,18,18,19,19,18,18,19,
  //   19,1a,1a,1b,1b,1a,1a,1b,1b,18,18,19,18,18,18,19,18,1a,1a,1b,1a,1a,1a,1b,1a,18,18,
  //   19,19,18,18,19,19,1a,1a,1b,1b,18,18,19,19,18,18,19,18,18,18,19,18,1a,1a,1b,1a,18,
  //   18,19,18,c,c,d,d,c,c,d,d,e,e,f,f,e,e,f,f,c,c,d,c,c,c,d,c,e,e,f,e,e,e,f,e,c,c,d,d,
  //   c,c,d,d,e,e,f,f,c,c,d,d,c,c,d,c,c,c,d,c,e,e,f,e,c,c,d,c,30,30,31,31,30,30,31,31,32,
  //   32,33,33,32,32,33,33,30,30,31,30,30,30,31,30,32,32,33,32,32,32,33,32,30,30,31,31,
  //   30,30,31,31,32,32,33,33,30,30,31,31,30,30,31,30,30,30,31,30,32,32,33,32,30,30,31,
  //   30,24,24,21,21,24,24,21,21,26,26,23,23,26,26,23,23,24,24,21,20,24,24,21,20,26,26,
  //   23,22,26,26,23,22,24,24,21,21,24,24,21,21,26,26,23,23,24,24,21,21,24,24,21,20,24,
  //   24,21,20,26,26,23,22,24,24,21,20,18,18,19,19,18,18,19,19,1a,1a,1b,1b,1a,1a,1b,1b,
  //   18,18,19,18,18,18,19,18,1a,1a,1b,1a,1a,1a,1b,1a,18,18,19,19,18,18,19,19,1a,1a,1b,
  //   1b,18,18,19,19,18,18,19,18,18,18,19,18,1a,1a,1b,1a,18,18,19,18,c,c,9,9,c,c,9,9,e,
  //   e,b,b,e,e,b,b,c,c,9,8,c,c,9,8,e,e,b,a,e,e,b,a,c,c,9,9,c,c,9,9,e,e,b,b,c,c,9,9,c,c,
  //   9,8,c,c,9,8,e,e,b,a,c,c,9,8,30,30,35,31,30,30,35,31,32,32,37,33,32,32,37,33,30,30,
  //   35,30,30,30,35,30,32,32,37,32,32,32,37,32,30,30,35,31,30,30,35,31,32,32,37,33,30,
  //   30,35,31,30,30,35,30,30,30,35,30,32,32,37,32,30,30,35,30,20,20,25,21,20,20,25,21,
  //   22,22,27,23,22,22,27,23,20,20,25,20,20,20,25,20,22,22,27,22,22,22,27,22,20,20,25,
  //   21,20,20,25,21,22,22,27,23,20,20,25,21,20,20,25,20,20,20,25,20,22,22,27,22,20,20,
  //   25,20,18,18,1d,19,18,18,1d,19,1a,1a,1f,1b,1a,1a,1f,1b,18,18,1d,18,18,18,1d,18,1a,
  //   1a,1f,1a,1a,1a,1f,1a,18,18,1d,19,18,18,1d,19,1a,1a,1f,1b,18,18,1d,19,18,18,1d,18,
  //   18,18,1d,18,1a,1a,1f,1a,18,18,1d,18,8,8,d,9,8,8,d,9,a,a,f,b,a,a,f,b,8,8,d,8,8,8,d,
  //   8,a,a,f,a,a,a,f,a,8,8,d,9,8,8,d,9,a,a,f,b,8,8,d,9,8,8,d,8,8,8,d,8,a,a,f,a,8,8,d,8,
  //   30,30,35,31,30,30,35,31,32,32,37,33,32,32,37,33,30,30,35,30,30,30,35,30,32,32,37,
  //   32,32,32,37,32,30,30,35,31,30,30,35,31,32,32,37,33,30,30,35,31,30,30,35,30,30,30,
  //   35,30,32,32,37,32,30,30,35,30,20,20,25,21,20,20,25,21,22,22,27,23,22,22,27,23,20,
  //   20,25,20,20,20,25,20,22,22,27,22,22,22,27,22,20,20,25,21,20,20,25,21,22,22,27,23,
  //   20,20,25,21,20,20,25,20,20,20,25,20,22,22,27,22,20,20,25,20,18,18,1d,19,18,18,1d,
  //   19,1a,1a,1f,1b,1a,1a,1f,1b,18,18,1d,18,18,18,1d,18,1a,1a,1f,1a,1a,1a,1f,1a,18,18,
  //   1d,19,18,18,1d,19,1a,1a,1f,1b,18,18,1d,19,18,18,1d,18,18,18,1d,18,1a,1a,1f,1a,18,
  //   18,1d,18,8,8,d,9,8,8,d,9,a,a,f,b,a,a,f,b,8,8,d,8,8,8,d,8,a,a,f,a,a,a,f,a,8,8,d,9,
  //   8,8,d,9,a,a,f,b,8,8,d,9,8,8,d,8,8,8,d,8,a,a,f,a,8,8,d,8,30,30,31,31,30,30,31,31,32,
  //   32,33,33,32,32,33,33,30,30,31,30,30,30,31,30,32,32,33,32,32,32,33,32,30,30,31,31,
  //   30,30,31,31,32,32,33,33,30,30,31,31,30,30,31,30,30,30,31,30,32,32,33,32,30,30,31,
  //   30,24,24,25,25,24,24,25,25,26,26,27,27,26,26,27,27,24,24,25,24,24,24,25,24,26,26,
  //   27,26,26,26,27,26,24,24,25,25,24,24,25,25,26,26,27,27,24,24,25,25,24,24,25,24,24,
  //   24,25,24,26,26,27,26,24,24,25,24,18,18,19,19,18,18,19,19,12,12,13,13,12,12,13,13,
  //   18,18,19,18,18,18,19,18,12,12,13,12,12,12,13,12,18,18,19,19,18,18,19,19,12,12,13,
  //   13,10,10,11,11,18,18,19,18,18,18,19,18,12,12,13,12,10,10,11,10,c,c,d,d,c,c,d,d,6,
  //   6,7,7,6,6,7,7,c,c,d,c,c,c,d,c,6,6,7,6,6,6,7,6,c,c,d,d,c,c,d,d,6,6,7,7,4,4,5,5,c,c,
  //   d,c,c,c,d,c,6,6,7,6,4,4,5,4,30,30,31,31,30,30,31,31,32,32,33,33,32,32,33,33,30,30,
  //   31,30,30,30,31,30,32,32,33,32,32,32,33,32,30,30,31,31,30,30,31,31,32,32,33,33,30,
  //   30,31,31,30,30,31,30,30,30,31,30,32,32,33,32,30,30,31,30,24,24,21,21,24,24,21,21,
  //   26,26,23,23,26,26,23,23,24,24,21,20,24,24,21,20,26,26,23,22,26,26,23,22,24,24,21,
  //   21,24,24,21,21,26,26,23,23,24,24,21,21,24,24,21,20,24,24,21,20,26,26,23,22,24,24,
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endmodule

/* Test case dbg_timmer:
CLK ~RST A     D     ~WE ~OE ~XINT0 ~XINT1  T0Q  T1Q
0    0   0     0x00  1   1   1      1       x	 x
C    1   0x8A  0xFD  0   1   1      1       x    x
C    1   0x8B  0xFE  0   1   1      1       x    x
C    1   0x8C  0xFF  0   1   1      1       x    x
C    1   0x8D  0xFF  0   1   1      1       x    x
C    1   0x89  0xC0  0   1   1      1       x    x
C    1   0x88  0x50  0   1   1      1       x    x

C    1   0x00  0x00  1   1   1      1       X      X 
C    1   0x00  0x00  1   1   1      1       0Xffff X
C    1   0x00  0x00  1   1   1      1       X      X 
C    1   0x00  0x00  1   1   1      1       X      X  
C    1   0x00  0x00  1   1   1      0       0Xffff X
C    1   0x00  0x00  1   1   1      1       X      0Xffff 
C    1   0x00  0x00  1   1   1      0       X      X  
C    1   0x00  0x00  1   1   1      1       0Xffff X
*/
