// Digital circuit RAM.dig as structural Verilog
// stop ouput clock if input S  is high. if go is 1, clock will ouput normally.
module RAM (
  input  CLK,
  input  [7:0] A,
  input  WE,
  input  nOE,
  input  Dt,
  output [7:0] O
);

  wire and_1_out, and_2_out, nand_1_out, not_1_out, not_4_out, not_5_out, not_6_out, not_7_out, or_1_out;
  wire [7:0] driver_2_out, driverinvsel_1_out, not_2_out, not_3_out, RAM_d;

  not not_1 (not_1_out, CLK);
  and and_1 (and_1_out, A[7], Dt);
  and and_2 (and_2_out, CLK, not_1_out);
  nand nand_1 (nand_1_out, WE, and_2_out);
  or or_1 (or_1_out, and_1_out, nOE);
  assign not_2_out = ~A;  // Not not_2, 8 bits wide
  assign not_3_out = ~not_2_out;  // Not not_3, 8 bits wide
  not not_4 (not_4_out, and_1_out);
  not not_5 (not_5_out, not_4_out);
  not not_6 (not_6_out, nOE);
  not not_7 (not_7_out, not_6_out);
  RAMSinglePortSel #(.AddrBits(8), .isProgramMemory("true"), .Bits(8)) RAM (
    .A(not_3_out), .CS(~not_5_out), .WE(~nand_1_out), .OE(~not_7_out), .D(RAM_d));
  assign driverinvsel_1_out = ~or_1_out ? RAM_d : 8'bz;  // DriverInvSel driverinvsel_1
  assign RAM_d = WE ? driver_2_out : 8'bz;  // Driver driver_1
  assign O = ~or_1_out ? driverinvsel_1_out : 8'bz;  // DriverInvSel driverinvsel_2
  assign driver_2_out = WE ? O : 8'bz;  // Driver driver_2

  // Notes on the sheet:
  //   A: address
  //   Dt: Direct address mode flag, it's will disable RAM when address is in
  //   0x80-0xFF.
  //   6116
  //   wait for the clock
  //   wait for the clock too
endmodule
