// Digital circuit RF_CTL.dig as structural Verilog
module RF_CTL (
  input  CLK,
  input  [7:0] BUS_D,
  input  [3:0] RF_SRC,
  input  RF_WE,
  input  RF_SFR,
  input  nRFSRCR_WE,
  input  nRAM_WE,
  input  nRAM_OE,
  output [3:0] ORF_SRC,
  output ORF_WE,
  output nORF_OE,
  output SFR_HIT
);

  wire [2:0] RFSRCR_q;
  wire [5:4] and_1_out;
  wire [7:4] RFSRCR_q_2;

  Register #(.Bits(8)) RFSRCR (.D(BUS_D), .C(CLK), .en(~nRFSRCR_WE), .Q({RFSRCR_q_2, SFR_HIT, RFSRCR_q}));
  and and_1 (and_1_out[4], SFR_HIT, nRAM_WE);
  nand nand_1 (and_1_out[5], SFR_HIT, ~nRAM_OE);  // NAnd
  Multiplexer #(.Bits(6)) multiplexer_1 (
    .sel(RF_SFR), .in_0({1'b1, RF_WE, RF_SRC}), .in_1({and_1_out, 1'b0, RFSRCR_q}),
    .out({nORF_OE, ORF_WE, ORF_SRC}));
endmodule
