// Digital circuit ROM.dig as structural Verilog
module ROM (
  input  [15:0] A,
  input  nOE,
  input  [7:0] IMMED,
  input  CLK,
  input  nPRRWE,
  input  [7:0] D,
  output [7:0] ROM_DB,
  output [15:0] IPRO_ADDR
);

  wire and_2_out, and_3_out, and_4_out, and_5_out, and_6_out, comparator_6_eq, comparator_7_eq,
       comparator_8_eq, comparator_9_eq, comparator_10_eq, comparator_11_eq, comparator_12_eq,
       comparator_13_eq, comparator_14_eq, comparator_15_eq, comparator_16_eq, comparator_17_eq,
       comparator_18_eq, comparator_19_eq, comparator_20_eq, comparator_21_eq, comparator_22_eq,
       comparator_23_eq, comparator_24_eq, comparator_25_eq, d_ff_1_nq, demultiplexer_1_out_0,
       demultiplexer_1_out_1, demultiplexer_1_out_2, demultiplexer_1_out_3, demultiplexer_1_out_4,
       demultiplexer_1_out_5, F_WC, haveData, nA_B, nand_1_out, nBUFCE, nCE, nor_2_out, nor_3_out, nor_4_out,
       nROM_WE, nWE, or_1_out, or_2_out, or_3_out, reset_1_out, ROM_WE, SDP_DE, SDP_DI, SDP_EN, timeoutBLC,
       tWC_to, WC_END, WC_WRITING;
  wire [2:2] PRR_q;
  wire [6:0] BUF_ADDR_d2;
  wire [7:0] BUF_DATA_d2, BUF_LEN, BUFF_D0, BUFF_D1, BUFF_D2, BUFF_D3, BUFF_D4, BUFF_D5, CNT_tBLC_out,
       sub_1_s, WEBUFFER_LEN_out;
  wire [8:0] d_ff_2_q;
  wire [15:0] BUFF_A0, BUFF_A1, BUFF_A2, BUFF_A3, BUFF_A4, BUFF_A5, CNT_tWC_out, sub_2_s;

  Register #(.Bits(3)) PRR (.D(IMMED[2:0]), .C(CLK), .en(~nPRRWE), .Q({PRR_q[2], nCE, nA_B}));
  nand nand_1 (nand_1_out, nA_B, nA_B);
  and and_1 (nBUFCE, nOE, nand_1_out);
  xor xor_1 (nWE, PRR_q[2], 1'b1);
  nor nor_1 (ROM_WE, nCE, nWE);
  not not_1 (nROM_WE, ROM_WE);
  and and_2 (and_2_out, timeoutBLC, haveData);
  D_FF d_ff_1 (.D(ROM_WE), .C(CLK), .nQ(d_ff_1_nq));  // open: Q
  Counter #(.Bits(8)) CNT_tBLC (.en(nROM_WE), .C(CLK), .clr(ROM_WE), .out(CNT_tBLC_out));  // open: ovf
  Sub #(.Bits(8)) sub_1 (.a(8'h64), .b(8'h1), .c_i(1'b0), .s(sub_1_s));  // open: c_o
  or or_1 (or_1_out, F_WC, and_2_out);
  nor nor_2 (nor_2_out, d_ff_1_nq, ROM_WE);
  // Probe on CNT_tBLC_out
  or or_2 (or_2_out, nBUFCE, ~nA_B);  // Or
  or or_3 (or_3_out, nBUFCE, nA_B);
  and and_3 (and_3_out, F_WC, WC_WRITING);
  Comparator #(.Bits(8)) comparator_1 (.a(CNT_tBLC_out), .b(sub_1_s), .eq(timeoutBLC));  // open: gt, lt
  Counter #(.Bits(16)) CNT_tWC (.en(or_1_out), .C(CLK), .clr(WC_END), .out(CNT_tWC_out));  // open: ovf
  assign D = ~or_3_out ? ROM_DB : 8'bz;  // DriverInvSel driverinvsel_1
  assign ROM_DB = ~or_2_out ? D : 8'bz;  // DriverInvSel driverinvsel_2
  Counter #(.Bits(8)) WEBUFFER_LEN (.en(and_3_out), .C(CLK), .clr(WC_END), .out(WEBUFFER_LEN_out));  // open: ovf
  Counter #(.Bits(8)) BUFFER_LEN (.en(nor_2_out), .C(CLK), .clr(WC_END), .out(BUF_LEN));  // open: ovf
  Sub #(.Bits(16)) sub_2 (.a(16'h1388), .b(16'h64), .c_i(1'b0), .s(sub_2_s));  // open: c_o
  Comparator #(.Bits(16)) comparator_2 (.a(CNT_tWC_out), .b({16{1'b0}}), .gt(F_WC));  // open: eq, lt
  Comparator #(.Bits(16)) comparator_3 (.a(CNT_tWC_out), .b(sub_2_s), .eq(tWC_to));  // open: gt, lt
  RAMDualAccess #(.AddrBits(8), .Bits(7)) BUF_ADDR (
    .str(1'b1), .C(ROM_WE), .ld(1'b1), .A1(BUF_LEN), .Din1(A[6:0]), .A2(WEBUFFER_LEN_out), .D2(BUF_ADDR_d2));  // open: D1
  RAMDualAccess #(.AddrBits(8), .Bits(8)) BUF_DATA (
    .str(1'b1), .C(nROM_WE), .ld(1'b1), .A1(BUF_LEN), .Din1(ROM_DB), .A2(WEBUFFER_LEN_out), .D2(BUF_DATA_d2));  // open: D1
  or or_4 (WC_END, tWC_to, SDP_DI, SDP_EN);
  nor nor_3 (nor_3_out, BUF_LEN[3], BUF_LEN[4], BUF_LEN[5], BUF_LEN[6], BUF_LEN[7]);
  Comparator #(.Bits(8)) comparator_4 (.a(WEBUFFER_LEN_out), .b(BUF_LEN), .lt(WC_WRITING));  // open: gt, eq
  Comparator #(.Bits(8)) comparator_5 (.a(BUF_LEN), .b({8{1'b0}}), .gt(haveData));  // open: eq, lt
  nor nor_4 (nor_4_out, nCE, nA_B);
  Demultiplexer #(.Selector_Bits(3)) demultiplexer_1 (
    .sel(BUF_LEN[2:0]), .in(nor_3_out), .out_0(demultiplexer_1_out_0), .out_1(demultiplexer_1_out_1),
    .out_2(demultiplexer_1_out_2), .out_3(demultiplexer_1_out_3), .out_4(demultiplexer_1_out_4),
    .out_5(demultiplexer_1_out_5));  // open: out_6, out_7
  D_FF #(.Bits(9)) d_ff_2 (.D(A[15:7]), .C(ROM_WE), .Q(d_ff_2_q));  // open: nQ
  and and_4 (and_4_out, F_WC, WC_WRITING, SDP_DE, reset_1_out);
  Reset reset_1 (.out(reset_1_out));
  Multiplexer #(.Bits(16)) multiplexer_1 (.sel(F_WC), .in_0(A), .in_1({d_ff_2_q, BUF_ADDR_d2}), .out(IPRO_ADDR));
  RS_FF #(.Default(1)) SDP_FLAG (.S(SDP_EN), .C(CLK), .R(SDP_DI), .nQ(SDP_DE));  // open: Q
  EEPROMDualPort #(.AddrBits(16), .isProgramMemory("true"), .Bits(8)) ROM (
    .A(IPRO_ADDR), .Din(BUF_DATA_d2), .str(and_4_out), .C(CLK), .ld(nor_4_out), .D(ROM_DB));
  Register #(.Bits(16)) SDP_ADDR0 (.D(A), .C(ROM_WE), .en(demultiplexer_1_out_0), .Q(BUFF_A0));
  Register #(.Bits(8)) register_1 (.D(ROM_DB), .C(nROM_WE), .en(demultiplexer_1_out_0), .Q(BUFF_D0));
  Register #(.Bits(16)) SDP_ADDR1 (.D(A), .C(ROM_WE), .en(demultiplexer_1_out_1), .Q(BUFF_A1));
  Register #(.Bits(8)) register_2 (.D(ROM_DB), .C(nROM_WE), .en(demultiplexer_1_out_1), .Q(BUFF_D1));
  Comparator #(.Bits(8)) comparator_6 (.a(BUFF_D0), .b(8'haa), .eq(comparator_6_eq));  // open: gt, lt
  Comparator #(.Bits(8)) comparator_7 (.a(BUFF_D1), .b(8'h55), .eq(comparator_7_eq));  // open: gt, lt
  Comparator #(.Bits(8)) comparator_8 (.a(BUFF_D2), .b(8'h80), .eq(comparator_8_eq));  // open: gt, lt
  Comparator #(.Bits(8)) comparator_9 (.a(BUFF_D3), .b(8'haa), .eq(comparator_9_eq));  // open: gt, lt
  Comparator #(.Bits(8)) comparator_10 (.a(BUFF_D4), .b(8'h55), .eq(comparator_10_eq));  // open: gt, lt
  Comparator #(.Bits(8)) comparator_11 (.a(BUFF_D5), .b(8'h20), .eq(comparator_11_eq));  // open: gt, lt
  Comparator #(.Bits(8)) comparator_12 (.a(BUF_LEN), .b(8'h5), .eq(comparator_12_eq));  // open: gt, lt
  Comparator #(.Bits(8)) comparator_13 (.a(BUFF_D0), .b(8'haa), .eq(comparator_13_eq));  // open: gt, lt
  Comparator #(.Bits(8)) comparator_14 (.a(BUFF_D1), .b(8'h55), .eq(comparator_14_eq));  // open: gt, lt
  Comparator #(.Bits(8)) comparator_15 (.a(BUFF_D2), .b(8'ha0), .eq(comparator_15_eq));  // open: gt, lt
  Comparator #(.Bits(8)) comparator_16 (.a(BUF_LEN), .b(8'h2), .eq(comparator_16_eq));  // open: gt, lt
  Register #(.Bits(16)) SDP_ADDR2 (.D(A), .C(ROM_WE), .en(demultiplexer_1_out_2), .Q(BUFF_A2));
  Register #(.Bits(8)) register_3 (.D(ROM_DB), .C(nROM_WE), .en(demultiplexer_1_out_2), .Q(BUFF_D2));
  and and_5 (and_5_out, comparator_6_eq, comparator_7_eq, comparator_8_eq, comparator_9_eq, comparator_10_eq, comparator_11_eq, comparator_12_eq);
  and and_6 (and_6_out, comparator_13_eq, comparator_14_eq, comparator_15_eq, comparator_16_eq);
  Register #(.Bits(16)) SDP_ADDR3 (.D(A), .C(ROM_WE), .en(demultiplexer_1_out_3), .Q(BUFF_A3));
  Register #(.Bits(8)) register_4 (.D(ROM_DB), .C(nROM_WE), .en(demultiplexer_1_out_3), .Q(BUFF_D3));
  Register #(.Bits(16)) SDP_ADDR4 (.D(A), .C(ROM_WE), .en(demultiplexer_1_out_4), .Q(BUFF_A4));
  Register #(.Bits(8)) register_5 (.D(ROM_DB), .C(nROM_WE), .en(demultiplexer_1_out_4), .Q(BUFF_D4));
  Comparator #(.Bits(16)) comparator_17 (.a(BUFF_A0), .b(16'h5555), .eq(comparator_17_eq));  // open: gt, lt
  Comparator #(.Bits(16)) comparator_18 (.a(BUFF_A1), .b(16'h2aaa), .eq(comparator_18_eq));  // open: gt, lt
  Comparator #(.Bits(16)) comparator_19 (.a(BUFF_A2), .b(16'h5555), .eq(comparator_19_eq));  // open: gt, lt
  Comparator #(.Bits(16)) comparator_20 (.a(BUFF_A3), .b(16'h5555), .eq(comparator_20_eq));  // open: gt, lt
  Comparator #(.Bits(16)) comparator_21 (.a(BUFF_A4), .b(16'h2aaa), .eq(comparator_21_eq));  // open: gt, lt
  Comparator #(.Bits(16)) comparator_22 (.a(BUFF_A5), .b(16'h5555), .eq(comparator_22_eq));  // open: gt, lt
  Comparator #(.Bits(16)) comparator_23 (.a(BUFF_A0), .b(16'h5555), .eq(comparator_23_eq));  // open: gt, lt
  Comparator #(.Bits(16)) comparator_24 (.a(BUFF_A1), .b(16'h2aaa), .eq(comparator_24_eq));  // open: gt, lt
  Comparator #(.Bits(16)) comparator_25 (.a(BUFF_A2), .b(16'h5555), .eq(comparator_25_eq));  // open: gt, lt
  Register #(.Bits(16)) SDP_ADDR5 (.D(A), .C(ROM_WE), .en(demultiplexer_1_out_5), .Q(BUFF_A5));
  Register #(.Bits(8)) register_6 (.D(ROM_DB), .C(nROM_WE), .en(demultiplexer_1_out_5), .Q(BUFF_D5));
  and and_7 (SDP_DI, and_5_out, comparator_17_eq, comparator_18_eq, comparator_19_eq, comparator_20_eq, comparator_21_eq, comparator_22_eq);
  and and_8 (SDP_EN, and_6_out, comparator_23_eq, comparator_24_eq, comparator_25_eq);

  // Other names for the same wires on the sheet: nOE_t = nA_B; A_buffer_byte[6:0] = A[6:0]; A_page[8:0] = A[15:7]

  // Notes on the sheet:
  //   A: address
  //   nOE: default 1
  //   CLK: Hz: 500
  //   nPRRWE: default 1
  //   IPRO_ADDR: address when internal programmer is writing the EEPROM
  //   contents of ROM (hex, n*v repeats v):
  //   0,0,0,0,0,0,0,0,0,0,0,0,0,0,0,0,0,0,0,0,0,0,0,0,0,0,0,0,0,0,0,0,0,0,0,0,0,0,0,0,0,
  //   0,0,0,0,0,0,0,0,0,0,0,0,0,0,0,0,0,0,0,0,0,0,0,0,0,0,0,0,0,0,0,0,0,0,0,0,0,0,0,0,0,
  //   0,0,0,0,0,0,0,0,0,0,0,0,0,0,0,0,0,0,0,0,0,0,0,0,0,0,0,0,0,0,0,0,0,0,0,0,0,0,0,0,0,
  //   0,0,0,0,ff,0,1,2,3,4,5,6,7,8,9,a,b,c,d,e,f,10,11,12,13,14,15,16,17,18,19,1a,1b,1c,
  //   1d,1e,1f,20,21,22,23,24,25,26,27,28,29,2a,2b,2c,2d,2e,2f,30,31,32,33,34,35,36,37,
  //   38,39,3a,3b,3c,3d,3e,3f,40,41,42,43,44,45,46,47,48,49,4a,4b,4c,4d,4e,4f,50,51,52,
  //   53,54,55,56,57,58,59,5a,5b,5c,5d,5e,5f,60,61,62,63,64,65,66,67,68,69,6a,6b,6c,6d,
  //   6e,6f,70,71,72,73,74,75,76,77,78,79,7a,7b,7c,7d,7e,7f,0,0,0,0,0,0,0,0,0,0,0,0,0,0,
  //   0,0,0,0,0,0,0,0,0,0,0,0,0,0,0,0,0,0,0,0,0,0,0,0,0,0,0,0,0,0,0,0,0,0,0,0,0,0,0,0,0,
  //   0,0,0,0,0,0,0,0,0,0,0,0,0,0,0,0,0,0,0,0,0,0,0,0,0,0,0,0,0,0,0,0,0,0,0,0,0,0,0,0,0,
  //   0,0,0,0,0,0,0,0,0,0,0,0,0,0,0,0,0,0,0,0,0,0,0,0,0,0,0,0,0,0,0,0,0,0,0,0,0,0,0,0,0,
  //   0,0,0,0,0,0,0,0,0,0,0,0,0,0,0,0,0,0,0,0,0,0,0,0,0,0,0,0,0,0,0,0,0,0,0,0,0,0,0,0,0,
  //   0,0,0,0,0,0,0,0,0,0,0,0,0,0,0,0,0,0,0,0,0,0,0,0,0,0,0,0,0,0,0,0,0,0,0,0,0,0,0,0,0,
  //   0,0,0,0,0,0,0,0,0,0,0,0,0,0,0,0,0,0,0,0,0,0,0,0,0,0,0,0,0,0,0,0,0,0,0,0,0,0,0,0,0,
  //   0,0,0,0,0,0,0,0,0,0,0,0,0,0,0,0,0,0,0,0,0,0,0,0,0,0,0,0,0,0,0,0,0,0,0,0,0,0,0,0,0,
  //   0,0,0,0,0,0,0,0,0,0,0,0,0,0,0,0,0,0,0,0,0,0,0,0,0,0,0,0,0,0,0,0,0,0,0,0,0,0,0,0,0,
  //   0,0,0,0,0,0,0,0,0,0,0,0,0,0,0,0,0,0,0,0,0,0,0,0,0,0,0,0,0,0,0,0,0,0,0,0,0,0,0,0,0,
  //   0,0,0,0,0,0,0,0,0,0,0,0,0,0,0,0,0,0,0,0,0,0,0,0,0,0,0,0,0,0,0,0,0,0,0,0,0,0,0,0,0,
  //   0,0,0,0,0,0,0,0,0,0,0,0,0,0,0,0,0,0,0,0,0,0,0,0,0,0,0,0,0,0,0,0,0,0,0,0,0,0,0,0,0,
  //   0,0,0,0,0,0,0,0,0,0,0,0,0,0,0,0,0,0,0,0,0,0,0,0,0,0,0,0,0,0,0,0,0,0,0,0,0,0,0,0,0,
  //   0,0,0,0,0,0,0,0,0,0,0,0,0,0,0,0,0,0,0,0,0,0,0,0,0,0,0,0,0,0,0,0,0,0,0,0,0,0,0,0,0,
  //   0,0,0,0,0,0,0,0,0,0,0,0,0,0,0,0,0,0,0,0,0,0,0,0,0,0,0,0,0,0,0,0,0,0,0,0,0,0,0,0,0,
  //   0,0,0,0,0,0,0,0,0,0,0,0,0,0,0,0,0,0,0,0,0,0,0,0,0,0,0,0,0,0,0,0,0,0,0,0,0,0,0,0,0,
  //   0,0,0,0,0,0,0,0,0,0,0,0,0,0,0,0,0,0,0,0,0,0,0,0,0,0,0,0,0,0,0,0,0,0,0,0,0,0,0,0,0,
  //   0,0,0,0,0,0,0,0,0,0,0,0,0,0,0,0,0,0,0,0,0,0,0,0,0,0,0,0,0,0,0,0,0,0,0,0,0,0,0,0,0,
  //   0,0,0,0,0,0,0,0,0,0,0,0,0,0,0,0,0,0,0,0,0,0,0,0,0,0,0,0,0,0,0,0,0,0,0,0,0,0,0,0,0,
  //   0,0,0,0,0,0,0,0,0,0,0,0,0,0,0,0,0,0,0,0,0,0,0,0,0,0,0,0,0,0,0,0,0,0,0,0,0,0,0,0,0,
  //   0,0,0,0,0,0,0,0,0,0,0,0,0,0,0,0,0,0,0,0,0,0,0,0,0,0,0,0,0,0,0,0,0,0,0,0,0,0,0,0,0,
  //   0,0,0,0,0,0,0,0,0,0,0,0,0,0,0,0,0,0,0,0,0,0,0,0,0,0,0,0,0,0,0,0,0,0,0,0,0,0,0,0,0,
  //   0,0,0,0,0,0,0,0,0,0,0,0,0,0,0,0,0,0,0,0,0,0,0,0,0,0,0,0,0,0,0,0,0,0,0,0,0,0,0,0,0,
  //   0,0,0,0,0,0,0,0,0,0,0,0,0,0,0,0,0,0,0,0,0,0,0,0,0,0,0,0,0,0,0,0,0,0,0,0,0,0,0,0,0,
  //   0,0,0,0,0,0,0,0,0,0,0,0,0,0,0,0,0,0,0,0,0,0,0,0,0,0,0,0,0,0,0,0,0,0,0,0,0,0,0,0,0,
  //   0,0,0,0,0,0,0,0,0,0,0,0,0,0,0,0,0,0,0,0,0,0,0,0,0,0,0,0,0,0,0,0,0,0,0,0,0,0,0,0,0,
  //   0,0,0,0,0,0,0,0,0,0,0,0,0,0,0,0,0,0,0,0,0,0,0,0,0,0,0,0,0,0,0,0,0,0,0,0,0,0,0,0,0,
  //   0,0,0,0,0,0,0,0,0,0,0,0,0,0,0,0,0,0,0,0,0,0,0,0,0,0,0,0,0,0,0,0,0,0,0,0,0,0,0,0,0,
  //   0,0,0,0,0,0,0,0,0,0,0,0,0,0,0,0,0,0,0,0,0,0,0,0,0,0,0,0,0,0,0,0,0,0,0,0,0,0,0,0,0,
  //   0,0,0,0,0,0,0,0,0,0,0,0,0,0,0,0,0,0,0,0,0,0,0,0,0,0,0,0,0,0,0,0,0,0,0,0,0,0,0,0,0,
  //   0,0,0,0,0,0,0,0,0,0,0,0,0,0,0,0,0,0,0,0,0,0,0,0,0,0,0,0,0,0,0,0,0,0,0,0,0,0,0,0,0,
  //   0,0,0,0,0,0,0,0,0,0,0,0,0,0,0,0,0,0,0,0,0,0,0,0,0,0,0,0,0,0,0,0,0,0,0,0,0,0,0,0,0,
  //   0,0,0,0,0,0,0,0,0,0,0,0,0,0,0,0,0,0,0,0,0,0,0,0,0,0,0,0,0,0,0,0,0,0,0,0,0,0,0,0,0,
  //   0,0,0,0,0,0,0,0,0,0,0,0,0,0,0,0,0,0,0,0,0,0,0,0,0,0,0,0,0,0,0,0,0,0,0,0,0,0,0,0,0,
  //   0,0,0,0,0,0,0,0,0,0,0,0,0,0,0,0,0,0,0,0,0,0,0,0,0,0,0,0,0,0,0,0,0,0,0,0,0,0,0,0,0,
  //   0,0,0,0,0,0,0,0,0,0,0,0,0,0,0,0,0,0,0,0,0,0,0,0,0,0,0,0,0,0,0,0,0,0,0,0,0,0,0,0,0,
  //   0,0,0,0,0,0,0,0,0,0,0,0,0,0,0,0,0,0,0,0,0,0,0,0,0,0,0,0,0,0,0,0,0,0,0,0,0,0,0,0,0,
  //   0,0,0,0,0,0,0,0,0,0,0,0,0,0,0,0,0,0,0,0,0,0,0,0,0,0,0,0,0,0,0,0,0,0,0,0,0,0,0,0,0,
  //   0,0,0,0,0,0,0,0,0,0,0,0,0,0,0,0,0,0,0,0,0,0,0,0,0,0,0,0,0,0,0,0,0,0,0,0,0,0,0,0,0,
  //   0,0,0,0,0,0,0,0,0,0,0,0,0,0,0,0,0,0,0,0,0,0,0,0,0,0,0,0,0,0,0,0,0,0,0,0,0,0,0,0,0,
  //   0,0,0,0,0,0,0,0,0,0,0,0,0,0,0,0,0,0,0,0,0,0,0,0,0,0,0,0,0,0,0,0,0,0,0,0,0,0,0,0,0,
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endmodule

/* Test case writeData:
CLK	A	D	IMMED	~PRRWE	~OE 	ROM_DB IPRO_ADDR
0	0	0	0	0	1	X	X
C	0	0	1	0	1	X	X

C	0x5555	0xAA	5	0	1	X	X
C	0x5555	0xAA	1	0	1	X	X
C	0x2AAA	0x55	5	0	1	X	X
C	0x2AAA	0x55	1	0	1	X	X
C	0x5555	0x80	5	0	1	X	X
C	0x5555	0x80	1	0	1	X	X
C	0x5555	0xAA	5	0	1	X	X
C	0x5555	0xAA	1	0	1	X	X
C	0x2AAA	0x55	5	0	1	X	X
C	0x2AAA	0x55	1	0	1	X	X
C	0x5555	0x20	5	0	1	X	X
C	0x5555	0x20	1	0	1	X	X

loop(a,128)
C	(a+128)	(a)	5	0	1	X	X
C	(a+128)	(a)	1	0	1	X	X
end loop

repeat(5000) 	C	0	0	0	1	1	X	X
		C	0	0	0	0	1	X	X

loop(a,128)
C	(a+128)	0	0	1	1	(a)	X
end loop

C	127		0xFF	5	0	1	X	X
C	127		0xFF	1	0	1	X	X

		
repeat(5000) 	C	0	0	0	1	1	X	X
		C	0	0	0	0	1	X	X

C	127     0	0	1	1	0xFF	X

loop(a,128)
C	(a+128)	0	0	1	1	(a)	X
end loop

C	0x5555	0xAA	5	0	1	X	X
C	0x5555	0xAA	1	0	1	X	X
C	0x2AAA	0x55	5	0	1	X	X
C	0x2AAA	0x55	1	0	1	X	X
C	0x5555	0xa0	5	0	1	X	X
C	0x5555	0xa0	1	0	1	X	X


C	127		0x12	5	0	1	X	X
C	127		0x12	1	0	1	X	X
		
repeat(5000) 	C	0	0	0	1	1	X	X
		C	0	0	0	0	1	X	X

C	127     0	0	1	1	0xFF	X

C	0x5555	0xAA	5	0	1	X	X
C	0x5555	0xAA	1	0	1	X	X
C	0x2AAA	0x55	5	0	1	X	X
C	0x2AAA	0x55	1	0	1	X	X
C	0x5555	0x80	5	0	1	X	X
C	0x5555	0x80	1	0	1	X	X
C	0x5555	0xAA	5	0	1	X	X
C	0x5555	0xAA	1	0	1	X	X
C	0x2AAA	0x55	5	0	1	X	X
C	0x2AAA	0x55	1	0	1	X	X
C	0x5555	0x20	5	0	1	X	X
C	0x5555	0x20	1	0	1	X	X
*/
