// Digital circuit SBUF.dig as structural Verilog
module SBUF (
  input  [7:0] IO,
  input  CLK,
  input  [7:0] A,
  input  OE,
  input  WE,
  output RI,
  output TI
);

  wire and_1_out, and_2_out, comparator_1_eq;
  wire [15:8] keyboard_1_d;

  Comparator #(.Bits(8)) comparator_1 (.a(A), .b(8'h99), .eq(comparator_1_eq));  // open: gt, lt
  and and_1 (and_1_out, comparator_1_eq, OE);
  and and_2 (and_2_out, comparator_1_eq, WE);
  Keyboard keyboard_1 (.C(CLK), .en(and_1_out), .D({keyboard_1_d, IO}), .av(RI));
  Terminal terminal_1 (.D(IO), .C(CLK), .en(and_2_out));
  Register register_1 (.D(and_2_out), .C(CLK), .en(and_2_out), .Q(TI));
endmodule
