// Digital circuit SCON.dig as structural Verilog
module SCON (
  input  CLK,
  input  CLR,
  input  [7:0] IO,
  input  [7:0] A,
  input  OE,
  input  WE,
  input  RI,
  input  TI,
  output TRI
);

  wire and_1_out, and_2_out, comparator_1_eq;
  wire [1:0] or_1_out;
  wire [7:0] multiplexer_1_out, reg__sync_clear_1_q;

  Comparator #(.Bits(8)) comparator_1 (.a(A), .b(8'h98), .eq(comparator_1_eq));  // open: gt, lt
  and and_1 (and_1_out, comparator_1_eq, OE);
  and and_2 (and_2_out, comparator_1_eq, WE);
  assign IO = and_1_out ? reg__sync_clear_1_q : 8'bz;  // Driver driver_1
  Multiplexer #(.Bits(8)) multiplexer_1 (
    .sel(and_2_out), .in_0(reg__sync_clear_1_q), .in_1(IO), .out(multiplexer_1_out));
  or or_1 (or_1_out[0], multiplexer_1_out[0], RI);
  or or_2 (or_1_out[1], TI, multiplexer_1_out[1]);
  reg__sync_clear #(.generic("Bits := 8;")) reg__sync_clear_1 (
    .D({multiplexer_1_out[7:2], or_1_out}), .CLK(CLK), .CLR(CLR), .nLE(1'b1), .Q(reg__sync_clear_1_q));
  or or_3 (TRI, reg__sync_clear_1_q[0], reg__sync_clear_1_q[1]);
endmodule
