// Digital circuit SFR_CTL.dig as structural Verilog
module SFR_CTL (
  input  nSFR_WE,
  input  nSFR_OE,
  input  [7:0] A,
  input  [7:0] MADDR,
  output nWE,
  output nOE
);

  wire comparator_1_eq, not_1_out;

  Comparator #(.Bits(8)) comparator_1 (.a(A), .b(MADDR), .eq(comparator_1_eq));  // open: gt, lt
  not not_1 (not_1_out, comparator_1_eq);
  or or_1 (nWE, nSFR_WE, not_1_out);
  or or_2 (nOE, not_1_out, nSFR_OE);
endmodule
