// Digital circuit SFR_GENERIC_REG.dig as structural Verilog
module SFR_GENERIC_REG (
  input  CLK,
  input  nRST,
  input  [7:0] A,
  input  [7:0] D,
  input  [7:0] SETB,
  input  [7:0] nCLRB,
  input  nSFR_WE,
  input  nSFR_OE,
  input  [7:0] MADDR,
  output [7:0] Q
);

  wire sfr_ctl_1_noe, sfr_ctl_1_nwe;

  SFR_CTL sfr_ctl_1 (
    .nSFR_WE(nSFR_WE), .nSFR_OE(nSFR_OE), .A(A), .MADDR(MADDR), .nWE(sfr_ctl_1_nwe), .nOE(sfr_ctl_1_noe));
  \reg  #(.generic("Bits := int(args.Bits);")) reg_1 (
    .D(D), .CLK(CLK), .nWE(sfr_ctl_1_nwe), .SETB(SETB), .nCLRB(nCLRB), .nRST(nRST), .Q(Q));
  assign D = ~sfr_ctl_1_noe ? Q : 8'bz;  // DriverInvSel driverinvsel_1

  // Notes on the sheet:
  //   CLK: CLOCK
  //   nRST: default 1
  //   A: default 1
  //   SETB: set REG[n] to 1 if  SETB[n] is 1
  //   nCLRB: set REG[n] to 0 if  CLRB[n] is 0, default 255
  //   nSFR_OE: set REG[n] to 0 if  CLRB[n] is 0, default 255
  //   MADDR: default 1
endmodule
