// Digital circuit SFR_SBUF.dig as structural Verilog
module SFR_SBUF (
  input  CLK,
  input  [7:0] D,
  input  nWE,
  input  nOE,
  output RI,
  output TI
);

  wire not_1_out;
  wire [15:8] keyboard_1_d;

  not not_1 (not_1_out, nWE);
  Keyboard keyboard_1 (.C(CLK), .en(~nOE), .D({keyboard_1_d, D}), .av(RI));
  Terminal terminal_1 (.D(D), .C(CLK), .en(not_1_out));
  Register register_1 (.D(not_1_out), .C(CLK), .en(not_1_out), .Q(TI));

  // Notes on the sheet:
  //   nWE: default 1
  //   nOE: default 1
endmodule
