// Digital circuit SFR_SCON.dig as structural Verilog
module SFR_SCON (
  input  CLK,
  input  nRST,
  input  [7:0] D,
  input  nWE,
  input  nOE,
  input  [1:0] IRQ,
  output [7:0] Q,
  output IRRQ
);

  \reg  #(.generic("Bits := 8;")) reg_1 (
    .D(D), .CLK(CLK), .nWE(nWE), .SETB({{6{1'b0}}, IRQ}), .nCLRB({8{1'b1}}), .nRST(nRST), .Q(Q));
  assign D = ~nOE ? Q : 8'bz;  // DriverInvSel driverinvsel_1
  or or_1 (IRRQ, Q[0], Q[1]);

  // Notes on the sheet:
  //   nRST: default 1
  //   IRRQ: IRRQ = RI + TI
  //   nWE: default 1
  //   nOE: default 1
  //   IRQ: IRQ[0] = RI, IRQ[1] = TI
endmodule
