// Digital circuit SFR_TIMMER.dig as structural Verilog
module SFR_TIMMER (
  input  CLK,
  input  nRST,
  input  [7:0] D,
  input  nWEL,
  input  nWEH,
  input  CNTEN,
  output OV
);

  wire not_1_out, or_1_out;
  wire [7:0] reg_1_q, reg_2_q;
  wire [15:0] add_1_s, multiplexer_1_out, register_1_q;

  not not_1 (not_1_out, CNTEN);
  \reg  #(.generic("Bits := 8;")) reg_1 (
    .D(D), .CLK(CLK), .nWE(nWEL), .SETB({8{1'b0}}), .nCLRB({8{1'b1}}), .nRST(nRST), .Q(reg_1_q));
  \reg  #(.generic("Bits := 8;")) reg_2 (
    .D(D), .CLK(CLK), .nWE(nWEH), .SETB({8{1'b0}}), .nCLRB({8{1'b1}}), .nRST(nRST), .Q(reg_2_q));
  or or_1 (or_1_out, not_1_out, OV);
  Multiplexer #(.Bits(16)) multiplexer_1 (
    .sel(or_1_out), .in_0(add_1_s), .in_1({reg_2_q, reg_1_q}), .out(multiplexer_1_out));
  // Probe TIMMERL on {reg_2_q, reg_1_q}
  Register #(.Bits(16)) register_1 (.D(multiplexer_1_out), .C(CLK), .en(1'b1), .Q(register_1_q));
  Add #(.Bits(16)) add_1 (.a(register_1_q), .b({16{1'b0}}), .c_i(1'b1), .s(add_1_s), .c_o(OV));
  // Probe CNTO on add_1_s

  // Notes on the sheet:
  //   nRST: default 1
  //   nWEL: default 1
  //   nWEH: default 1
  //   CNTEN: default 1
  //   CNT_EN
endmodule
