// Digital circuit STALL.dig as structural Verilog
// Stop output clock if  Stall  is high. 
// If this is a raising edge ocurres in Go, clock will output normally.
module STALL (
  input  Stall,
  input  Go,
  input  nCLR,
  input  SW,
  input  CLK_manual,
  input  CLK_in,
  output CLK,
  output CLK_async
);

  wire and_1_out, and_2_out, and_3_out, and_4_out, and_5_out, and_6_out, CLK_switch, comparator_1_eq,
       comparator_3_eq, delay_1_out, INTR_q, not_1_out, not_2_out, not_3_out, not_4_out, or_1_out, or_2_out,
       register_1_q, register_2_q, SYNC0_q, SYNC1_q, SYNC_MC_q, SYNC_SW_q;
  wire [3:0] counter_1_out;

  Counter #(.Bits(4)) counter_1 (.en(1'b1), .C(CLK_in), .clr(comparator_1_eq), .out(counter_1_out));  // open: ovf
  Register SYNC_SW (.D(SW), .C(CLK_switch), .en(1'b1), .Q(SYNC_SW_q));
  Register SYNC_MC (.D(CLK_manual), .C(CLK_switch), .en(1'b1), .Q(SYNC_MC_q));
  Comparator #(.Bits(4)) comparator_1 (.a(counter_1_out), .b(4'b1011), .eq(comparator_1_eq));  // open: gt, lt
  Comparator #(.Bits(4)) comparator_2 (.a(counter_1_out), .b(4'b0110), .eq(CLK_switch));  // open: gt, lt
  Comparator #(.Bits(4)) comparator_3 (.a(counter_1_out), .b(4'b0000), .eq(comparator_3_eq));  // open: gt, lt
  Register register_1 (.D(SYNC_MC_q), .C(CLK_switch), .en(1'b1), .Q(register_1_q));
  // Probe CLK_SW on CLK_switch
  not not_1 (not_1_out, register_1_q);
  and and_1 (and_1_out, SYNC_MC_q, not_1_out);
  not not_2 (not_2_out, comparator_3_eq);
  Register SYNC0 (.D(Go), .C(not_2_out), .en(1'b1), .Q(SYNC0_q));
  Register SYNC1 (.D(SYNC0_q), .C(not_2_out), .en(1'b1), .Q(SYNC1_q));
  Register register_2 (.D(SYNC1_q), .C(not_2_out), .en(1'b1), .Q(register_2_q));
  not not_3 (not_3_out, SYNC1_q);
  or or_1 (or_1_out, INTR_q, Stall);
  or or_2 (or_2_out, register_2_q, not_3_out);
  and and_2 (and_2_out, or_1_out, nCLR, or_2_out);
  Register INTR (.D(and_2_out), .C(not_2_out), .en(1'b1), .Q(INTR_q));
  not not_4 (not_4_out, INTR_q);
  and and_3 (and_3_out, comparator_1_eq, not_4_out);
  and and_4 (and_4_out, comparator_3_eq, not_4_out);
  Delay delay_1 (.in(and_4_out), .out(delay_1_out));
  and and_5 (and_5_out, and_3_out, and_1_out);
  and and_6 (and_6_out, delay_1_out, and_1_out);
  Multiplexer multiplexer_1 (.sel(SYNC_SW_q), .in_0(and_3_out), .in_1(and_5_out), .out(CLK_async));
  Multiplexer multiplexer_2 (.sel(SYNC_SW_q), .in_0(delay_1_out), .in_1(and_6_out), .out(CLK));

  // Notes on the sheet:
  //   CLK: main clock
  //   Stall: stop clock
  //   Go: continue clock. enable CLKO when detected raise edge. sync with ~CLKI
  //   CLK_async: clock to generate write pulse for async RAM
  //   nCLR: stop clock
  //   SW: switch of manual and crystal clock.
  //   set 1 to usign manual clock
  //   CLK_manual: manual clock
  //   postive edge check
endmodule
