// Digital circuit TOP.dig as structural Verilog
module TOP (
  input  CLK,
  input  [11:0] MIPCBI,
  input  MIPCBE,
  input  [15:0] PCBIA1,
  input  PCBE1,
  input  [15:0] PCBIA2,
  input  PCBE2,
  input  [31:0] in_10,
  output CLK_2,
  output [7:0] BUS_D,
  output [11:0] MIPC
);

  wire and_2_out, and_3_out, and_4_out, AST_FAIL, button_1_out, button_4_out, button_5_out, comparator_1_eq,
       comparator_2_eq, comparator_3_eq, core_1_p16, dipswitch_1_out, DUMP_p5, EXIT_p5, GENCLKBRK, IRQ, nCLR,
       nINT1, nIRR_CLR, nITN0, nSFR_OE, nSFR_WE, or_1_out, reset_1_out;
  wire [3:0] register_1_q, register_1_q_2, register_2_q, register_2_q_2, register_3_q, register_3_q_2,
       register_4_q, register_4_q_2, register_5_q, register_6_q, register_6_q_2, register_7_q,
       register_7_q_2, register_8_q, register_8_q_2;
  wire [7:0] ADDR_SFR, opcode_q, PORT0_q, PORT1_q;
  wire [7:4] register_5_q_2;
  wire [15:0] PC;
  wire [23:0] counter_1_out;
  wire [31:0] add_1_s, add_2_s, add_3_s, op_count_d, op_tick_total_d, op_tickcnt_out, tick_total;

  // ASSERT ASSERT: pin names not known; wires that end beside it: CLK_2, ADDR_SFR, BUS_D, nSFR_WE, AST_FAIL
  // EXTCTL EXIT: pin names not known; wires that end beside it: CLK_2, ADDR_SFR, BUS_D, nSFR_WE, EXIT_p5
  // DUMP DUMP: pin names not known; wires that end beside it: CLK_2, ADDR_SFR, BUS_D, nSFR_WE, DUMP_p5
  // PER_INT_IO per_int_io_1: pin names not known; wires that end beside it: CLK_2, nCLR, ADDR_SFR, BUS_D, nSFR_WE, nSFR_OE, nIRR_CLR, nITN0, nINT1, IRQ
  // Probe on EXIT_p5
  // Probe on DUMP_p5
  // Probe on IRQ
  // Probe on PC
  // Probe on MIPC
  SFR_GENERIC_REG #(.generic("Bits := 8;")) PORT1 (
    .CLK(CLK_2), .nRST(nCLR), .A(ADDR_SFR), .D(BUS_D), .SETB({8{1'b0}}), .nCLRB({8{1'b1}}),
    .nSFR_WE(nSFR_WE), .nSFR_OE(nSFR_OE), .MADDR(8'h90), .Q(PORT1_q));
  SFR_GENERIC_REG #(.generic("Bits := 8;")) PORT0 (
    .CLK(CLK_2), .nRST(nCLR), .A(ADDR_SFR), .D(BUS_D), .SETB({8{1'b0}}), .nCLRB({8{1'b1}}),
    .nSFR_WE(nSFR_WE), .nSFR_OE(nSFR_OE), .MADDR(8'h80), .Q(PORT0_q));
  Button #(.activeLow("true")) button_1 (.out(button_1_out));
  Button #(.activeLow("true")) button_2 (.out(nITN0));
  Button #(.activeLow("true")) button_3 (.out(nINT1));
  Comparator #(.Bits(12)) comparator_1 (.a(MIPCBI), .b(MIPC), .eq(comparator_1_eq));  // open: gt, lt
  Comparator #(.Bits(16)) comparator_2 (.a(PCBIA1), .b(PC), .eq(comparator_2_eq));  // open: gt, lt
  Comparator #(.Bits(16)) comparator_3 (.a(PCBIA2), .b(PC), .eq(comparator_3_eq));  // open: gt, lt
  Reset reset_1 (.out(reset_1_out));
  and and_1 (nCLR, reset_1_out, button_1_out);
  and and_2 (and_2_out, comparator_1_eq, MIPCBE);
  and and_3 (and_3_out, comparator_2_eq, PCBE1);
  and and_4 (and_4_out, comparator_3_eq, PCBE2);
  Seven_Seg #(.ledPersistence("true"), .commonConnectionType("anode")) seven_seg_1 (
    .a(register_1_q[0]), .b(register_1_q[1]), .c(register_1_q[2]), .d(register_1_q[3]),
    .e(register_1_q_2[0]), .f(register_1_q_2[1]), .g(register_1_q_2[2]), .dp(register_1_q_2[3]));
  DipSwitch dipswitch_1 (.out(dipswitch_1_out));
  Register #(.Bits(8)) register_1 (.D(PORT1_q), .C(PORT0_q[7]), .en(1'b1), .Q({register_1_q_2, register_1_q}));
  Button button_4 (.out(button_4_out));
  Button button_5 (.out(button_5_out));
  or or_1 (or_1_out, and_2_out, and_3_out, and_4_out, AST_FAIL, GENCLKBRK);
  Seven_Seg #(.ledPersistence("true"), .commonConnectionType("anode")) seven_seg_2 (
    .a(register_2_q[0]), .b(register_2_q[1]), .c(register_2_q[2]), .d(register_2_q[3]),
    .e(register_2_q_2[0]), .f(register_2_q_2[1]), .g(register_2_q_2[2]), .dp(register_2_q_2[3]));
  // CORE core_1: pin names not known; wires that end beside it: CLK, nCLR, IRQ, button_4_out, dipswitch_1_out, button_5_out, or_1_out, PC, MIPC, CLK_2, BUS_D, ADDR_SFR, nSFR_WE, nSFR_OE, nIRR_CLR, core_1_p16
  Register #(.Bits(8)) register_2 (.D(PORT1_q), .C(PORT0_q[6]), .en(1'b1), .Q({register_2_q_2, register_2_q}));
  Counter #(.Bits(32)) tickcnt (.en(~or_1_out), .C(CLK_2), .clr(~nCLR), .out(tick_total));  // open: ovf
  Comparator #(.Bits(32)) comparator_4 (.a(tick_total), .b(in_10), .eq(GENCLKBRK));  // open: gt, lt
  Seven_Seg #(.ledPersistence("true"), .commonConnectionType("anode")) seven_seg_3 (
    .a(register_3_q[0]), .b(register_3_q[1]), .c(register_3_q[2]), .d(register_3_q[3]),
    .e(register_3_q_2[0]), .f(register_3_q_2[1]), .g(register_3_q_2[2]), .dp(register_3_q_2[3]));
  Register #(.Bits(8)) register_3 (.D(PORT1_q), .C(PORT0_q[5]), .en(1'b1), .Q({register_3_q_2, register_3_q}));
  // Probe tick_total on tick_total
  Seven_Seg #(.ledPersistence("true"), .commonConnectionType("anode")) seven_seg_4 (
    .a(register_4_q[0]), .b(register_4_q[1]), .c(register_4_q[2]), .d(register_4_q[3]),
    .e(register_4_q_2[0]), .f(register_4_q_2[1]), .g(register_4_q_2[2]), .dp(register_4_q_2[3]));
  Register #(.Bits(8)) register_4 (.D(PORT1_q), .C(PORT0_q[4]), .en(1'b1), .Q({register_4_q_2, register_4_q}));
  Seven_Seg #(.ledPersistence("true"), .commonConnectionType("anode")) seven_seg_5 (
    .a(register_5_q[0]), .b(register_5_q[1]), .c(register_5_q[2]), .d(register_5_q[3]),
    .e(register_5_q_2[4]), .f(register_5_q_2[5]), .g(register_5_q_2[6]), .dp(register_5_q_2[7]));
  // Probe on BUS_D
  Register #(.Bits(8)) opcode (.D(BUS_D), .C(CLK_2), .en(core_1_p16), .Q(opcode_q));
  Counter #(.Bits(32)) op_tickcnt (.en(1'b1), .C(CLK_2), .clr(core_1_p16), .out(op_tickcnt_out));  // open: ovf
  Register #(.Bits(8)) register_5 (.D(PORT1_q), .C(PORT0_q[3]), .en(1'b1), .Q({register_5_q_2, register_5_q}));
  // Probe on op_tickcnt_out
  Seven_Seg #(.ledPersistence("true"), .commonConnectionType("anode")) seven_seg_6 (
    .a(register_6_q[0]), .b(register_6_q[1]), .c(register_6_q[2]), .d(register_6_q[3]),
    .e(register_6_q_2[0]), .f(register_6_q_2[1]), .g(register_6_q_2[2]), .dp(register_6_q_2[3]));
  Counter #(.Bits(24)) counter_1 (.en(core_1_p16), .C(CLK_2), .clr(~nCLR), .out(counter_1_out));  // open: ovf
  Add #(.Bits(32)) add_1 (.a(op_tickcnt_out), .b(32'h1), .c_i(1'b0), .s(add_1_s));  // open: c_o
  Register #(.Bits(8)) register_6 (.D(PORT1_q), .C(PORT0_q[2]), .en(1'b1), .Q({register_6_q_2, register_6_q}));
  Add #(.Bits(32)) add_2 (.a(add_1_s), .b(op_tick_total_d), .c_i(1'b0), .s(add_2_s));  // open: c_o
  Seven_Seg #(.ledPersistence("true"), .commonConnectionType("anode")) seven_seg_7 (
    .a(register_7_q[0]), .b(register_7_q[1]), .c(register_7_q[2]), .d(register_7_q[3]),
    .e(register_7_q_2[0]), .f(register_7_q_2[1]), .g(register_7_q_2[2]), .dp(register_7_q_2[3]));
  RAMDualPort #(.AddrBits(24), .Bits(16)) PCtrace (
    .A(counter_1_out), .Din(PC), .str(core_1_p16), .C(CLK_2), .ld(1'b1));  // open: D
  RAMDualPort #(.AddrBits(8), .Bits(32)) op_count (
    .A(BUS_D), .Din(add_3_s), .str(core_1_p16), .C(CLK_2), .ld(1'b1), .D(op_count_d));
  Register #(.Bits(8)) register_7 (.D(PORT1_q), .C(PORT0_q[1]), .en(1'b1), .Q({register_7_q_2, register_7_q}));
  // Probe on opcode_q
  Seven_Seg #(.ledPersistence("true"), .commonConnectionType("anode")) seven_seg_8 (
    .a(register_8_q[0]), .b(register_8_q[1]), .c(register_8_q[2]), .d(register_8_q[3]),
    .e(register_8_q_2[0]), .f(register_8_q_2[1]), .g(register_8_q_2[2]), .dp(register_8_q_2[3]));
  Add #(.Bits(32)) add_3 (.a(32'h1), .b(op_count_d), .c_i(1'b0), .s(add_3_s));  // open: c_o
  RAMDualPort #(.AddrBits(8), .Bits(32)) op_tick_total (
    .A(opcode_q), .Din(add_2_s), .str(core_1_p16), .C(CLK_2), .ld(1'b1), .D(op_tick_total_d));
  RAMDualPort #(.AddrBits(8), .Bits(32)) op_tick_aver (
    .A(opcode_q), .Din(add_1_s), .str(core_1_p16), .C(CLK_2), .ld(1'b1));  // open: D
  Register #(.Bits(8)) register_8 (.D(PORT1_q), .C(PORT0_q[0]), .en(1'b1), .Q({register_8_q_2, register_8_q}));

  // Other names for the same wires on the sheet: CLK_t = CLK_2

  // Notes on the sheet:
  //   CLK: Hz: 2147483647
  //   MIPCBI: default 521
  //   PCBIA1: default 1407
  //   in_10: default 4294967295
  //   contents of ROM (hex, n*v repeats v):
  //   75,d0,2,90,ff,0,2,10,0,0,0,0,0,0,0,0,0,0,0,0,0,0,0,0,0,0,0,0,0,0,0,0,0,0,0,0,0,0, 0,0,0,0,0,
  //   0,0,0,0,0,0,0,0,0,0,0,0,0,0,0,0,0,0,0,0,0,0,0,0,0,0,0,0,0,0,0,0,0,0,0,0, 0,0,0,0,0,0,0,0,0,
  //   0,0,0,0,0,0,0,0,0,0,0,0,0,0,0,0,0,0,0,0,0,0,0,0,0,0,0,0,0,0,0,0, 0,0,0,0,0,0,0,0,0,0,0,0,0,
  //   0,0,0,0,0,0,0,0,0,0,0,0,0,0,0,0,0,0,0,0,0,0,0,0,0,0,0,0, 0,0,0,0,0,0,0,0,0,0,0,0,0,0,0,0,0,
  //   0,0,0,0,0,0,0,0,0,0,0,0,0,0,0,0,0,0,0,0,0,0,0,0, 0,0,0,0,0,0,0,0,0,0,0,0,0,0,0,0,0,0,0,0,0,
  //   0,0,0,0,0,0,0,0,0,0,0,0,0,0,0,0,0,0,0,0, 0,0,0,0,0,0,0,0,0,0,0,0,0,0,0,0,0,0,0,0,0,0,0,0,0,
  //   0,0,0,0,0,0,0,0,0,0,0,0,0,0,0,0, 0,0,0,0,0,0,0,0,0,0,0,0,0,0,0,0,0,0,0,0,0,0,0,0,0,0,0,0,0,
  //   0,0,0,0,0,0,0,0,0,0,0,0, 0,0,0,0,0,0,0,0,0,0,0,0,0,0,0,0,0,0,0,0,0,0,0,0,0,0,0,0,0,0,0,0,0,
  //   0,0,0,0,0,0,0,0, 0,0,0,0,0,0,0,0,0,0,0,0,0,0,0,0,0,0,0,0,0,0,0,0,0,0,0,0,0,0,0,0,0,0,0,0,0,
  //   0,0,0,0, 0,0,0,0,0,0,0,0,0,0,0,0,0,0,0,0,0,0,0,0,0,0,0,0,0,0,0,0,0,0,0,0,0,0,0,0,0,0,0,0,0,
  //    0,0,0,0,0,0,0,0,0,0,0,0,0,0,0,0,0,0,0,0,0,0,0,0,0,0,0,0,0,0,0,0,0,0,0,0,0,0,0,0,0, 0,0,0,0,
  //   0,0,0,0,0,0,0,0,0,0,0,0,0,0,0,0,0,0,0,0,0,0,0,0,0,0,0,0,0,0,0,0,0,0,0,0,0, 0,0,0,0,0,0,0,0,
  //   0,0,0,0,0,0,0,0,0,0,0,0,0,0,0,0,0,0,0,0,0,0,0,0,0,0,0,0,0,0,0,0,0, 0,0,0,0,0,0,0,0,0,0,0,0,
  //   0,0,0,0,0,0,0,0,0,0,0,0,0,0,0,0,0,0,0,0,0,0,0,0,0,0,0,0,0, 0,0,0,0,0,0,0,0,0,0,0,0,0,0,0,0,
  //   0,0,0,0,0,0,0,0,0,0,0,0,0,0,0,0,0,0,0,0,0,0,0,0,0, 0,0,0,0,0,0,0,0,0,0,0,0,0,0,0,0,0,0,0,0,
  //   0,0,0,0,0,0,0,0,0,0,0,0,0,0,0,0,0,0,0,0,0, 0,0,0,0,0,0,0,0,0,0,0,0,0,0,0,0,0,0,0,0,0,0,0,0,
  //   0,0,0,0,0,0,0,0,0,0,0,0,0,0,0,0,0, 0,0,0,0,0,0,0,0,0,0,0,0,0,0,0,0,0,0,0,0,0,0,0,0,0,0,0,0,
  //   0,0,0,0,0,0,0,0,0,0,0,0,0, 0,0,0,0,0,0,0,0,0,0,0,0,0,0,0,0,0,0,0,0,0,0,0,0,0,0,0,0,0,0,0,0,
  //   0,0,0,0,0,0,0,0,0, 0,0,0,0,0,0,0,0,0,0,0,0,0,0,0,0,0,0,0,0,0,0,0,0,0,0,0,0,0,0,0,0,0,0,0,0,
  //   0,0,0,0,0, 0,0,0,0,0,0,0,0,0,0,0,0,0,0,0,0,0,0,0,0,0,0,0,0,0,0,0,0,0,0,0,0,0,0,0,0,0,0,0,0,
  //   0, 0,0,0,0,0,0,0,0,0,0,0,0,0,0,0,0,0,0,0,0,0,0,0,0,0,0,0,0,0,0,0,0,0,0,0,0,0,0,0,0,0, 0,0,0,
  //   0,0,0,0,0,0,0,0,0,0,0,0,0,0,0,0,0,0,0,0,0,0,0,0,0,0,0,0,0,0,0,0,0,0,0,0,0,0, 0,0,0,0,0,0,0,
  //   0,0,0,0,0,0,0,0,0,0,0,0,0,0,0,0,0,0,0,0,0,0,0,0,0,0,0,0,0,0,0,0,0,0, 0,0,0,0,0,0,0,0,0,0,0,
  //   0,0,0,0,0,0,0,0,0,0,0,0,0,0,0,0,0,0,0,0,0,0,0,0,0,0,0,0,0,0, 0,0,0,0,0,0,0,0,0,0,0,0,0,0,0,
  //   0,0,0,0,0,0,0,0,0,0,0,0,0,0,0,0,0,0,0,0,0,0,0,0,0,0, 0,0,0,0,0,0,0,0,0,0,0,0,0,0,0,0,0,0,0,
  //   0,0,0,0,0,0,0,0,0,0,0,0,0,0,0,0,0,0,0,0,0,0, 0,0,0,0,0,0,0,0,0,0,0,0,0,0,0,0,0,0,0,0,0,0,0,
  //   0,0,0,0,0,0,0,0,0,0,0,0,0,0,0,0,0,0, 0,0,0,0,0,0,0,0,0,0,0,0,0,0,0,0,0,0,0,0,0,0,0,0,0,0,0,
  //   0,0,0,0,0,0,0,0,0,0,0,0,0,0, 0,0,0,0,0,0,0,0,0,0,0,0,0,0,0,0,0,0,0,0,0,0,0,0,0,0,0,0,0,0,0,
  //   0,0,0,0,0,0,0,0,0,0, 0,0,0,0,0,0,0,0,0,0,0,0,0,0,0,0,0,0,0,0,0,0,0,0,0,0,0,0,0,0,0,0,0,0,0,
  //   0,0,0,0,0,0, 0,0,0,0,0,0,0,0,0,0,0,0,0,0,0,0,0,0,0,0,0,0,0,0,0,0,0,0,0,0,0,0,0,0,0,0,0,0,0,
  //   0,0, 0,0,0,0,0,0,0,0,0,0,0,0,0,0,0,0,0,0,0,0,0,0,0,0,0,0,0,0,0,0,0,0,0,0,0,0,0,0,0,0,0, 0,0,
  //   0,0,0,0,0,0,0,0,0,0,0,0,0,0,0,0,0,0,0,0,0,0,0,0,0,0,0,0,0,0,0,0,0,0,0,0,0,0,0, 0,0,0,0,0,0,
  //   0,0,0,0,0,0,0,0,0,0,0,0,0,0,0,0,0,0,0,0,0,0,0,0,0,0,0,0,0,0,0,0,0,0,0, 0,0,0,0,0,0,0,0,0,0,
  //   0,0,0,0,0,0,0,0,0,0,0,0,0,0,0,0,0,0,0,0,0,0,0,0,0,0,0,0,0,0,0, 0,0,0,0,0,0,0,0,0,0,0,0,0,0,
  //   0,0,0,0,0,0,0,0,0,0,0,0,0,0,0,0,0,0,0,0,0,0,0,0,0,0,0, 0,0,0,0,0,0,0,0,0,0,0,0,0,0,0,0,0,0,
  //   0,0,0,0,0,0,0,0,0,0,0,0,0,0,0,0,0,0,0,0,0,0,0, 0,0,0,0,0,0,0,0,0,0,0,0,0,0,0,0,0,0,0,0,0,0,
  //   0,0,0,0,0,0,0,0,0,0,0,0,0,0,0,0,0,0,0, 0,0,0,0,0,0,0,0,0,0,0,0,0,0,0,0,0,0,0,0,0,0,0,0,0,0,
  //   0,0,0,0,0,0,0,0,0,0,0,0,0,0,0, 0,0,0,0,0,0,0,0,0,0,0,0,0,0,0,0,0,0,0,0,0,0,0,0,0,0,0,0,0,0,
  //   0,0,0,0,0,0,0,0,0,0,0, 0,0,0,0,0,0,0,0,0,0,0,0,0,0,0,0,0,0,0,0,0,0,0,0,0,0,0,0,0,0,0,0,0,0,
  //   0,0,0,0,0,0,0, 0,0,0,0,0,0,0,0,0,0,0,0,0,0,0,0,0,0,0,0,0,0,0,0,0,0,0,0,0,0,0,0,0,0,0,0,0,0,
  //   0,0,0, 0,0,0,0,0,0,0,0,0,0,0,0,0,0,0,0,0,0,0,0,0,0,0,0,0,0,0,0,0,0,0,0,0,0,0,0,0,0,0,0,0, 0,
  //   0,0,0,0,0,0,0,0,0,0,0,0,0,0,0,0,0,0,0,0,0,0,0,0,0,0,0,0,0,0,0,0,0,0,0,0,0,0,0,0, 0,0,0,0,0,
  //   0,0,0,0,0,0,0,0,0,0,0,0,0,0,0,0,0,0,0,0,0,0,0,0,0,0,0,0,0,0,0,0,0,0,0,0, 0,0,0,0,0,0,0,0,0,
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  //   contents of ALUDL (hex, n*v repeats v):
  //   10,21,42,83,4,5,6,7,18,29,4a,8b,c,d,e,f,1,30,53,92,15,14,17,16,9,38,5b,9a,1d,1c,1f, 1e,32,3,
  //   60,a1,26,27,24,25,3a,b,68,a9,2e,2f,2c,2d,23,12,71,b0,37,36,35,34,2b,1a,79, b8,3f,3e,3d,3c,54,
  //   65,6,c7,40,41,42,43,5c,6d,e,cf,48,49,4a,4b,45,74,17,d6,51,50,53, 52,4d,7c,1f,de,59,58,5b,5a,
  //   76,47,24,e5,62,63,60,61,7e,4f,2c,ed,6a,6b,68,69,67,56, 35,f4,73,72,71,70,6f,5e,3d,fc,7b,7a,
  //   79,78,98,a9,ca,b,8c,8d,8e,8f,90,a1,c2,3,84,85, 86,87,89,b8,db,1a,9d,9c,9f,9e,81,b0,d3,12,95,
  //   94,97,96,ba,8b,e8,29,ae,af,ac,ad,b2, 83,e0,21,a6,a7,a4,a5,ab,9a,f9,38,bf,be,bd,bc,a3,92,f1,
  //   30,b7,b6,b5,b4,dc,ed,8e,4f, c8,c9,ca,cb,d4,e5,86,47,c0,c1,c2,c3,cd,fc,9f,5e,d9,d8,db,da,c5,
  //   f4,97,56,d1,d0,d3, d2,fe,cf,ac,6d,ea,eb,e8,e9,f6,c7,a4,65,e2,e3,e0,e1,ef,de,bd,7c,fb,fa,f9,
  //   f8,e7,d6, b5,74,f3,f2,f1,f0,0,1,2,3,4,5,6,7,8,9,80,81,82,83,84,85,0,1,2,3,4,5,6,7,8,9,80,81,
  //    82,83,84,85,0,1,2,3,4,5,6,7,8,9,80,81,82,83,84,85,0,1,2,3,4,5,6,7,8,9,80,81,82,83, 84,85,0,
  //   1,2,3,4,5,6,7,8,9,80,81,82,83,84,85,0,1,2,3,4,5,6,7,8,9,80,81,82,83,84,85, 0,1,2,3,4,5,6,7,
  //   8,9,80,81,82,83,84,85,0,1,2,3,4,5,6,7,8,9,80,81,82,83,84,85,6,7,48, 49,4a,4b,4c,4d,e,f,80,81,
  //   82,83,84,85,6,7,48,49,4a,4b,4c,4d,e,f,80,81,82,83,84,85, 6,7,48,49,4a,4b,4c,4d,e,f,80,81,82,
  //   83,84,85,6,7,48,49,4a,4b,4c,4d,e,f,80,81,82,83, 84,85,6,7,48,49,4a,4b,4c,4d,e,f,80,81,82,83,
  //   84,85,6,7,48,49,4a,4b,4c,4d,e,f,80,81, 82,83,84,85,6,7,48,49,4a,4b,4c,4d,e,f,80,81,82,83,84,
  //   85,6,7,48,49,4a,4b,4c,4d,e,f, 80,81,82,83,84,85,0,1,2,3,4,5,6,7,8,9,a,b,c,d,e,f,1,2,3,4,5,6,
  //   7,48,9,a,b,c,d,e,f, 80,2,3,4,5,6,7,48,49,a,b,c,d,e,f,80,81,3,4,5,6,7,48,49,4a,b,c,d,e,f,80,
  //   81,82,4,5, 6,7,48,49,4a,4b,c,d,e,f,80,81,82,83,5,6,7,48,49,4a,4b,4c,d,e,f,80,81,82,83,84,6,
  //   7, 48,49,4a,4b,4c,4d,e,f,80,81,82,83,84,85,7,48,49,4a,4b,4c,4d,4e,f,80,81,82,83,84,85, 86,8,
  //   9,a,b,c,d,e,f,c0,c1,c2,c3,c4,c5,c6,c7,9,a,b,c,d,e,f,80,c1,c2,c3,c4,c5,c6,c7, 88,a,b,c,d,e,f,
  //   80,81,c2,c3,c4,c5,c6,c7,88,89,b,c,d,e,f,80,81,82,c3,c4,c5,c6,c7,88, 89,8a,c,d,e,f,80,81,82,
  //   83,c4,c5,c6,c7,88,89,8a,8b,d,e,f,80,81,82,83,84,c5,c6,c7,88, 89,8a,8b,8c,e,f,80,81,82,83,84,
  //   85,c6,c7,88,89,8a,8b,8c,8d,f,80,81,82,83,84,85,86, c7,88,89,8a,8b,8c,8d,8e,0,1,2,3,4,5,6,7,
  //   8,9,a,b,c,d,e,f,8f,0,1,2,3,4,5,6,47,8,9,a, b,c,d,e,8e,8f,0,1,2,3,4,5,46,47,8,9,a,b,c,d,8d,8e,
  //   8f,0,1,2,3,4,45,46,47,8,9,a,b,c, 8c,8d,8e,8f,0,1,2,3,44,45,46,47,8,9,a,b,8b,8c,8d,8e,8f,0,1,
  //   2,43,44,45,46,47,8,9,a, 8a,8b,8c,8d,8e,8f,0,1,42,43,44,45,46,47,8,9,89,8a,8b,8c,8d,8e,8f,0,
  //   41,42,43,44,45, 46,47,8,c8,c9,ca,cb,cc,cd,ce,cf,0,1,2,3,4,5,6,7,87,c8,c9,ca,cb,cc,cd,ce,8f,
  //   0,1,2, 3,4,5,6,86,87,c8,c9,ca,cb,cc,cd,8e,8f,0,1,2,3,4,5,85,86,87,c8,c9,ca,cb,cc,8d,8e,8f, 0,
  //   1,2,3,4,84,85,86,87,c8,c9,ca,cb,8c,8d,8e,8f,0,1,2,3,83,84,85,86,87,c8,c9,ca,8b, 8c,8d,8e,8f,
  //   0,1,2,82,83,84,85,86,87,c8,c9,8a,8b,8c,8d,8e,8f,0,1,81,82,83,84,85,86, 87,c8,89,8a,8b,8c,8d,
  //   8e,8f,0,0,81,82,3,84,5,6,87,88,9,a,8b,c,8d,8e,f,0,81,82,3,84, 5,6,87,88,9,a,8b,c,8d,8e,f,0,
  //   81,82,3,84,5,6,87,88,9,a,8b,c,8d,8e,f,0,81,82,3,84,5, 6,87,88,9,a,8b,c,8d,8e,f,0,81,82,3,84,
  //   5,6,87,88,9,a,8b,c,8d,8e,f,0,81,82,3,84,5,6, 87,88,9,a,8b,c,8d,8e,f,0,81,82,3,84,5,6,87,88,
  //   9,a,8b,c,8d,8e,f,0,81,82,3,84,5,6,87, 88,9,a,8b,c,8d,8e,f,0,81,82,3,84,5,6,87,88,9,a,8b,c,8d,
  //   8e,f,0,81,82,3,84,5,6,87,88, 9,a,8b,c,8d,8e,f,0,81,82,3,84,5,6,87,88,9,a,8b,c,8d,8e,f,0,81,
  //   82,3,84,5,6,87,88,9, a,8b,c,8d,8e,f,0,81,82,3,84,5,6,87,88,9,a,8b,c,8d,8e,f,0,81,82,3,84,5,
  //   6,87,88,9,a, 8b,c,8d,8e,f,0,81,82,3,84,5,6,87,88,9,a,8b,c,8d,8e,f,0,81,82,3,84,5,6,87,88,9,
  //   a,8b, c,8d,8e,f,0,11,20,31,40,51,60,71,80,91,a0,b1,c0,d1,e0,f1,10,11,30,31,50,51,70,71, 90,
  //   91,b0,b1,d0,d1,f0,f1,20,31,20,31,60,71,60,71,a0,b1,a0,b1,e0,f1,e0,f1,30,31,30, 31,70,71,70,
  //   71,b0,b1,b0,b1,f0,f1,f0,f1,40,51,60,71,40,51,60,71,c0,d1,e0,f1,c0,d1, e0,f1,50,51,70,71,50,
  //   51,70,71,d0,d1,f0,f1,d0,d1,f0,f1,60,71,60,71,60,71,60,71,e0, f1,e0,f1,e0,f1,e0,f1,70,71,70,
  //   71,70,71,70,71,f0,f1,f0,f1,f0,f1,f0,f1,88,99,a8,b9, c8,d9,e8,f9,88,99,a8,b9,c8,d9,e8,f9,98,
  //   99,b8,b9,d8,d9,f8,f9,98,99,b8,b9,d8,d9,f8, f9,a8,b9,a8,b9,e8,f9,e8,f9,a8,b9,a8,b9,e8,f9,e8,
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  //   contents of ALUS (hex, n*v repeats v):
  //   0,1,2,3,4,5,6,7,40,41,42,43,44,45,46,47,10,11,12,13,14,15,16,17,50,51,52,53,54,55, 56,57,20,
  //   21,22,23,24,25,26,27,60,61,62,63,64,65,66,67,30,31,32,33,34,35,36,37,70, 71,72,73,74,75,76,
  //   77,8,9,a,b,c,d,e,f,48,49,4a,4b,4c,4d,4e,4f,18,19,1a,1b,1c,1d,1e, 1f,58,59,5a,5b,5c,5d,5e,5f,
  //   28,29,2a,2b,2c,2d,2e,2f,68,69,6a,6b,6c,6d,6e,6f,38,39, 3a,3b,3c,3d,3e,3f,78,79,7a,7b,7c,7d,
  //   7e,7f,80,81,82,83,84,85,86,87,c0,c1,c2,c3,c4, c5,c6,c7,90,91,92,93,94,95,96,97,d0,d1,d2,d3,
  //   d4,d5,d6,d7,a0,a1,a2,a3,a4,a5,a6,a7, e0,e1,e2,e3,e4,e5,e6,e7,b0,b1,b2,b3,b4,b5,b6,b7,f0,f1,
  //   f2,f3,f4,f5,f6,f7,88,89,8a, 8b,8c,8d,8e,8f,c8,c9,ca,cb,cc,cd,ce,cf,98,99,9a,9b,9c,9d,9e,9f,
  //   d8,d9,da,db,dc,dd, de,df,a8,a9,aa,ab,ac,ad,ae,af,e8,e9,ea,eb,ec,ed,ee,ef,b8,b9,ba,bb,bc,bd,
  //   be,bf,f8, f9,fa,fb,fc,fd,fe,ff,3,b,13,1b,23,2b,33,3b,3,b,13,1b,23,2b,33,3b,3,b,13,1b,23,2b,
  //    33,3b,3,b,13,1b,23,2b,33,3b,3,b,13,1b,23,2b,33,3b,3,b,13,1b,23,2b,33,3b,3,b,13,1b, 23,2b,33,
  //   3b,3,b,13,1b,23,2b,33,3b,3,b,13,1b,23,2b,33,3b,3,b,13,1b,23,2b,33,3b,3,b, 13,1b,23,2b,33,3b,
  //   3,b,13,1b,23,2b,33,3b,3,b,13,1b,23,2b,33,3b,3,b,13,1b,23,2b,33, 3b,3,b,13,1b,23,2b,33,3b,3,
  //   b,13,1b,23,2b,33,3b,3,b,13,1b,23,2b,33,3b,3,b,13,1b,23, 2b,33,3b,3,b,13,1b,23,2b,33,3b,3,b,
  //   13,1b,23,2b,33,3b,3,b,13,1b,23,2b,33,3b,3,b,13, 1b,23,2b,33,3b,3,b,13,1b,23,2b,33,3b,3,b,13,
  //   1b,23,2b,33,3b,3,b,13,1b,23,2b,33,3b, 3,b,13,1b,23,2b,33,3b,3,b,13,1b,23,2b,33,3b,3,b,13,1b,
  //   23,2b,33,3b,3,b,13,1b,23,2b, 33,3b,3,b,13,1b,23,2b,33,3b,3,b,13,1b,23,2b,33,3b,3,b,13,1b,23,
  //   2b,33,3b,0,1,2,3,4, 5,6,7,8,9,a,b,c,d,e,f,10,11,12,13,14,15,16,17,18,19,1a,1b,1c,1d,1e,1f,20,
  //   21,22,23, 24,25,26,27,28,29,2a,2b,2c,2d,2e,2f,30,31,32,33,34,35,36,37,38,39,3a,3b,3c,3d,3e,
  //    3f,40,41,42,43,44,45,46,47,48,49,4a,4b,4c,4d,4e,4f,50,51,52,53,54,55,56,57,58,59, 5a,5b,5c,
  //   5d,5e,5f,60,61,62,63,64,65,66,67,68,69,6a,6b,6c,6d,6e,6f,70,71,72,73,74, 75,76,77,78,79,7a,
  //   7b,7c,7d,7e,7f,80,81,82,83,84,85,86,87,88,89,8a,8b,8c,8d,8e,8f, 90,91,92,93,94,95,96,97,98,
  //   99,9a,9b,9c,9d,9e,9f,a0,a1,a2,a3,a4,a5,a6,a7,a8,a9,aa, ab,ac,ad,ae,af,b0,b1,b2,b3,b4,b5,b6,
  //   b7,b8,b9,ba,bb,bc,bd,be,bf,c0,c1,c2,c3,c4,c5, c6,c7,c8,c9,ca,cb,cc,cd,ce,cf,d0,d1,d2,d3,d4,
  //   d5,d6,d7,d8,d9,da,db,dc,dd,de,df,e0, e1,e2,e3,e4,e5,e6,e7,e8,e9,ea,eb,ec,ed,ee,ef,f0,f1,f2,
  //   f3,f4,f5,f6,f7,f8,f9,fa,fb, fc,fd,fe,ff,0,0,0,0,0,0,0,0,0,0,0,0,0,0,0,0,0,0,0,0,0,0,0,0,0,0,
  //   0,0,0,0,0,0,0,0,0, 0,0,0,0,0,0,0,0,0,0,0,0,0,0,0,0,0,0,0,0,0,0,0,0,0,0,0,0,0,0,0,0,0,0,0,0,
  //   0,0,0,0,0, 0,0,0,0,0,0,0,0,0,0,0,0,0,0,0,0,0,0,0,0,0,0,0,0,0,0,0,0,0,0,0,0,0,0,0,0,0,0,0,0,
  //   0, 0,0,0,0,0,0,0,0,0,0,0,0,8,9,a,0,0,0,0,0,0,0,0,0,0,0,0,0,0,0,0,0,0,0,0,0,0,0,0,0,0, 0,0,0,
  //   0,0,0,0,0,0,0,b,0,0,0,0,0,0,0,0,0,0,0,0,0,0,0,c,0,0,0,0,0,0,0,0,0,0,0,0,0,0, 0,0,0,0,0,0,0,
  //   0,0,d,0,0,0,0,0,0,0,0,0,0,0,0,0,0,0,e,0,0,0,0,0,0,0,0,0,0,0,0,0,0,0, f,0,0,0,0,0,0,0,0,0,0,
  //   0,0,0,0,0,0,80,1,81,2,82,3,83,4,84,5,85,6,86,7,87,8,88,9,89, a,8a,b,8b,c,8c,d,8d,e,8e,f,8f,
  //   10,90,11,91,12,92,13,93,14,94,15,95,16,96,17,97,18, 98,19,99,1a,9a,1b,9b,1c,9c,1d,9d,1e,9e,
  //   1f,9f,20,a0,21,a1,22,a2,23,a3,24,a4,25,a5, 26,a6,27,a7,28,a8,29,a9,2a,aa,2b,ab,2c,ac,2d,ad,
  //   2e,ae,2f,af,30,b0,31,b1,32,b2,33, b3,34,b4,35,b5,36,b6,37,b7,38,b8,39,b9,3a,ba,3b,bb,3c,bc,
  //   3d,bd,3e,be,3f,bf,40,c0, 41,c1,42,c2,43,c3,44,c4,45,c5,46,c6,47,c7,48,c8,49,c9,4a,ca,4b,cb,
  //   4c,cc,4d,cd,4e, ce,4f,cf,50,d0,51,d1,52,d2,53,d3,54,d4,55,d5,56,d6,57,d7,58,d8,59,d9,5a,da,
  //   5b,db, 5c,dc,5d,dd,5e,de,5f,df,60,e0,61,e1,62,e2,63,e3,64,e4,65,e5,66,e6,67,e7,68,e8,69, e9,
  //   6a,ea,6b,eb,6c,ec,6d,ed,6e,ee,6f,ef,70,f0,71,f1,72,f2,73,f3,74,f4,75,f5,76,f6, 77,f7,78,f8,
  //   79,f9,7a,fa,7b,fb,7c,fc,7d,fd,7e,fe,7f,ff,0,2,4,6,8,a,c,e,10,12,14,16, 18,1a,1c,1e,20,22,24,
  //   26,28,2a,2c,2e,30,32,34,36,38,3a,3c,3e,40,42,44,46,48,4a,4c, 4e,50,52,54,56,58,5a,5c,5e,60,
  //   62,64,66,68,6a,6c,6e,70,72,74,76,78,7a,7c,7e,80,82, 84,86,88,8a,8c,8e,90,92,94,96,98,9a,9c,
  //   9e,a0,a2,a4,a6,a8,aa,ac,ae,b0,b2,b4,b6,b8, ba,bc,be,c0,c2,c4,c6,c8,ca,cc,ce,d0,d2,d4,d6,d8,
  //   da,dc,de,e0,e2,e4,e6,e8,ea,ec,ee, f0,f2,f4,f6,f8,fa,fc,fe,1,3,5,7,9,b,d,f,11,13,15,17,19,1b,
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  //   contents of ALUDH (hex, n*v repeats v):
  //   0,1,2,3,14,25,46,87,8,9,a,b,1c,2d,4e,8f,11,10,13,12,5,34,57,96,19,18,1b,1a,d,3c,5f, 9e,22,23,
  //   20,21,36,7,64,a5,2a,2b,28,29,3e,f,6c,ad,33,32,31,30,27,16,75,b4,3b,3a,39, 38,2f,1e,7d,bc,44,
  //   45,46,47,50,61,2,c3,4c,4d,4e,4f,58,69,a,cb,55,54,57,56,41,70,13, d2,5d,5c,5f,5e,49,78,1b,da,
  //   66,67,64,65,72,43,20,e1,6e,6f,6c,6d,7a,4b,28,e9,77,76, 75,74,63,52,31,f0,7f,7e,7d,7c,6b,5a,
  //   39,f8,88,89,8a,8b,9c,ad,ce,f,80,81,82,83,94,a5, c6,7,99,98,9b,9a,8d,bc,df,1e,91,90,93,92,85,
  //   b4,d7,16,aa,ab,a8,a9,be,8f,ec,2d,a2,a3, a0,a1,b6,87,e4,25,bb,ba,b9,b8,af,9e,fd,3c,b3,b2,b1,
  //   b0,a7,96,f5,34,cc,cd,ce,cf,d8, e9,8a,4b,c4,c5,c6,c7,d0,e1,82,43,dd,dc,df,de,c9,f8,9b,5a,d5,
  //   d4,d7,d6,c1,f0,93,52, ee,ef,ec,ed,fa,cb,a8,69,e6,e7,e4,e5,f2,c3,a0,61,ff,fe,fd,fc,eb,da,b9,
  //   78,f7,f6,f5, f4,e3,d2,b1,70,0,1,2,3,4,5,6,7,8,9,80,81,82,83,84,85,0,1,2,3,4,5,6,7,8,9,80,81,
  //   82, 83,84,85,0,1,2,3,4,5,6,7,8,9,80,81,82,83,84,85,0,1,2,3,4,5,6,7,8,9,80,81,82,83,84, 85,0,
  //   1,2,3,4,5,6,7,8,9,80,81,82,83,84,85,0,1,2,3,4,5,6,7,8,9,80,81,82,83,84,85,0, 1,2,3,4,5,6,7,
  //   8,9,80,81,82,83,84,85,0,1,2,3,4,5,6,7,8,9,80,81,82,83,84,85,6,7,48, 49,4a,4b,4c,4d,e,f,80,81,
  //   82,83,84,85,6,7,48,49,4a,4b,4c,4d,e,f,80,81,82,83,84,85, 6,7,48,49,4a,4b,4c,4d,e,f,80,81,82,
  //   83,84,85,6,7,48,49,4a,4b,4c,4d,e,f,80,81,82,83, 84,85,6,7,48,49,4a,4b,4c,4d,e,f,80,81,82,83,
  //   84,85,6,7,48,49,4a,4b,4c,4d,e,f,80,81, 82,83,84,85,6,7,48,49,4a,4b,4c,4d,e,f,80,81,82,83,84,
  //   85,6,7,48,49,4a,4b,4c,4d,e,f, 80,81,82,83,84,85,0,1,2,3,4,5,6,7,8,9,a,b,c,d,e,f,1,2,3,4,5,6,
  //   7,48,9,a,b,c,d,e,f, 80,2,3,4,5,6,7,48,49,a,b,c,d,e,f,80,81,3,4,5,6,7,48,49,4a,b,c,d,e,f,80,
  //   81,82,4,5, 6,7,48,49,4a,4b,c,d,e,f,80,81,82,83,5,6,7,48,49,4a,4b,4c,d,e,f,80,81,82,83,84,6,
  //   7, 48,49,4a,4b,4c,4d,e,f,80,81,82,83,84,85,7,48,49,4a,4b,4c,4d,4e,f,80,81,82,83,84,85, 86,8,
  //   9,a,b,c,d,e,f,c0,c1,c2,c3,c4,c5,c6,c7,9,a,b,c,d,e,f,80,c1,c2,c3,c4,c5,c6,c7, 88,a,b,c,d,e,f,
  //   80,81,c2,c3,c4,c5,c6,c7,88,89,b,c,d,e,f,80,81,82,c3,c4,c5,c6,c7,88, 89,8a,c,d,e,f,80,81,82,
  //   83,c4,c5,c6,c7,88,89,8a,8b,d,e,f,80,81,82,83,84,c5,c6,c7,88, 89,8a,8b,8c,e,f,80,81,82,83,84,
  //   85,c6,c7,88,89,8a,8b,8c,8d,f,80,81,82,83,84,85,86, c7,88,89,8a,8b,8c,8d,8e,0,1,2,3,4,5,6,7,
  //   8,9,a,b,c,d,e,f,8f,0,1,2,3,4,5,6,47,8,9,a, b,c,d,e,8e,8f,0,1,2,3,4,5,46,47,8,9,a,b,c,d,8d,8e,
  //   8f,0,1,2,3,4,45,46,47,8,9,a,b,c, 8c,8d,8e,8f,0,1,2,3,44,45,46,47,8,9,a,b,8b,8c,8d,8e,8f,0,1,
  //   2,43,44,45,46,47,8,9,a, 8a,8b,8c,8d,8e,8f,0,1,42,43,44,45,46,47,8,9,89,8a,8b,8c,8d,8e,8f,0,
  //   41,42,43,44,45, 46,47,8,c8,c9,ca,cb,cc,cd,ce,cf,0,1,2,3,4,5,6,7,87,c8,c9,ca,cb,cc,cd,ce,8f,
  //   0,1,2, 3,4,5,6,86,87,c8,c9,ca,cb,cc,cd,8e,8f,0,1,2,3,4,5,85,86,87,c8,c9,ca,cb,cc,8d,8e,8f, 0,
  //   1,2,3,4,84,85,86,87,c8,c9,ca,cb,8c,8d,8e,8f,0,1,2,3,83,84,85,86,87,c8,c9,ca,8b, 8c,8d,8e,8f,
  //   0,1,2,82,83,84,85,86,87,c8,c9,8a,8b,8c,8d,8e,8f,0,1,81,82,83,84,85,86, 87,c8,89,8a,8b,8c,8d,
  //   8e,8f,0,0,81,82,3,84,5,6,87,88,9,a,8b,c,8d,8e,f,0,81,82,3,84, 5,6,87,88,9,a,8b,c,8d,8e,f,0,
  //   81,82,3,84,5,6,87,88,9,a,8b,c,8d,8e,f,0,81,82,3,84,5, 6,87,88,9,a,8b,c,8d,8e,f,0,81,82,3,84,
  //   5,6,87,88,9,a,8b,c,8d,8e,f,0,81,82,3,84,5,6, 87,88,9,a,8b,c,8d,8e,f,0,81,82,3,84,5,6,87,88,
  //   9,a,8b,c,8d,8e,f,0,81,82,3,84,5,6,87, 88,9,a,8b,c,8d,8e,f,0,81,82,3,84,5,6,87,88,9,a,8b,c,8d,
  //   8e,f,0,81,82,3,84,5,6,87,88, 9,a,8b,c,8d,8e,f,0,81,82,3,84,5,6,87,88,9,a,8b,c,8d,8e,f,0,81,
  //   82,3,84,5,6,87,88,9, a,8b,c,8d,8e,f,0,81,82,3,84,5,6,87,88,9,a,8b,c,8d,8e,f,0,81,82,3,84,5,
  //   6,87,88,9,a, 8b,c,8d,8e,f,0,81,82,3,84,5,6,87,88,9,a,8b,c,8d,8e,f,0,81,82,3,84,5,6,87,88,9,
  //   a,8b, c,8d,8e,f,0,10,20,30,40,50,60,70,80,90,a0,b0,c0,d0,e0,f0,11,11,31,31,51,51,71,71, 91,
  //   91,b1,b1,d1,d1,f1,f1,20,30,20,30,60,70,60,70,a0,b0,a0,b0,e0,f0,e0,f0,31,31,31, 31,71,71,71,
  //   71,b1,b1,b1,b1,f1,f1,f1,f1,40,50,60,70,40,50,60,70,c0,d0,e0,f0,c0,d0, e0,f0,51,51,71,71,51,
  //   51,71,71,d1,d1,f1,f1,d1,d1,f1,f1,60,70,60,70,60,70,60,70,e0, f0,e0,f0,e0,f0,e0,f0,71,71,71,
  //   71,71,71,71,71,f1,f1,f1,f1,f1,f1,f1,f1,80,90,a0,b0, c0,d0,e0,f0,80,90,a0,b0,c0,d0,e0,f0,91,
  //   91,b1,b1,d1,d1,f1,f1,91,91,b1,b1,d1,d1,f1, f1,a0,b0,a0,b0,e0,f0,e0,f0,a0,b0,a0,b0,e0,f0,e0,
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  //   contents of DECODER (hex, n*v repeats v):
  //   800340155900,95f15854fb00,92f25914fb00,95f15854fc00,92f25914fc00,95f15854f500,92f25914f500,
  //    95f15854f400,92f25914f400,95f15854f300,92f25914f300,95f15854ee00,92f25914ee00,95f15854e900,
  //    92f25914e900,95f15854e900,92f25914e900,95f15854e500,92f25914e500,95f15854e500,92f25914e500,
  //    95f15854e500,92f25914e500,95f15854e500,92f25914e500,95f15854e500,92f25914e500,95f15854e500,
  //    92f25914e500,95f15854e500,92f25914e500,95f15854e500,92f25914e500,95f15854d700,92f25914d700,
  //    95f158550100,92f259150100,95f15854cc00,92f25914cc00,95f15854c900,92f25914c900,95f15854c800,
  //    92f25914c800,95f15854c200,92f25914c200,95f15854bd00,92f25914bd00,95f15854bd00,92f25914bd00,
  //    95f15854b900,92f25914b900,95f15854b900,92f25914b900,95f15854b900,92f25914b900,95f15854b900,
  //    92f25914b900,95f15854b900,92f25914b900,95f15854b900,92f25914b900,95f15854b900,92f25914b900,
  //    95f15854b900,92f25914b900,95f15854ae00,92f25914ae00,95f15854fc00,92f25914fc00,95f15854a900,
  //    92f25914a900,95f15854a800,92f25914a800,95f15854a100,92f25914a100,95f158549700,92f259149700,
  //    95f158548d00,92f259148d00,95f158548d00,92f259148d00,95f158548400,92f259148400,95f158548400,
  //    92f259148400,95f158548400,92f259148400,95f158548400,92f259148400,95f158548400,92f259148400,
  //    95f158548400,92f259148400,95f158548400,92f259148400,95f158548400,92f259148400,95f158547900,
  //    92f259147900,95f158550100,92f259150100,95f158547300,92f259147300,95f158547000,92f259147000,
  //    95f158546800,92f259146800,95f158545d00,92f259145d00,95f158545300,92f259145300,95f158545300,
  //    92f259145300,95f158544a00,92f259144a00,95f158544a00,92f259144a00,95f158544a00,92f259144a00,
  //    95f158544a00,92f259144a00,95f158544a00,92f259144a00,95f158544a00,92f259144a00,95f158544a00,
  //    92f259144a00,95f158544a00,92f259144a00,95f158544700,92f259144700,95f15854fc00,92f25914fc00,
  //    95f158544200,92f259144200,95f158543900,92f259143900,95f158543700,92f259143700,95f158543300,
  //    92f259143300,95f158542e00,92f259142e00,95f158542e00,92f259142e00,95f158542a00,92f259142a00,
  //    95f158542a00,92f259142a00,95f158542a00,92f259142a00,95f158542a00,92f259142a00,95f158542a00,
  //    92f259142a00,95f158542a00,92f259142a00,95f158542a00,92f259142a00,95f158542a00,92f259142a00,
  //    95f158542700,92f259142700,95f158550100,92f259150100,95f158542200,92f259142200,95f158541900,
  //    92f259141900,95f158541700,92f259141700,95f158541300,92f259141300,95f158540e00,92f259140e00,
  //    95f158540e00,92f259140e00,95f158540a00,92f259140a00,95f158540a00,92f259140a00,95f158540a00,
  //    92f259140a00,95f158540a00,92f259140a00,95f158540a00,92f259140a00,95f158540a00,92f259140a00,
  //    95f158540a00,92f259140a00,95f158540a00,92f259140a00,95f158540700,92f259140700,95f15854fc00,
  //    92f25914fc00,95f158540200,92f259140200,95f15853f900,92f25913f900,95f15853f700,92f25913f700,
  //    95f15853f300,92f25913f300,95f15853ee00,92f25913ee00,95f15853ee00,92f25913ee00,95f15853ea00,
  //    92f25913ea00,95f15853ea00,92f25913ea00,95f15853ea00,92f25913ea00,95f15853ea00,92f25913ea00,
  //    95f15853ea00,92f25913ea00,95f15853ea00,92f25913ea00,95f15853ea00,92f25913ea00,95f15853ea00,
  //    92f25913ea00,95f15853e700,92f25913e700,95f158550100,92f259150100,95f15853de00,92f25913de00,
  //    95f15853d900,92f25913d900,95f15853d800,92f25913d800,95f15853d100,92f25913d100,95f15853cc00,
  //    92f25913cc00,95f15853cc00,92f25913cc00,95f15853c800,92f25913c800,95f15853c800,92f25913c800,
  //    95f15853c800,92f25913c800,95f15853c800,92f25913c800,95f15853c800,92f25913c800,95f15853c800,
  //    92f25913c800,95f15853c800,92f25913c800,95f15853c800,92f25913c800,95f15853c300,92f25913c300,
  //    95f15854fc00,92f25914fc00,95f15853ba00,92f25913ba00,95f15853b600,92f25913b600,95f158538400,
  //    92f259138400,95f158537a00,92f259137a00,95f158537200,92f259137200,95f158537200,92f259137200,
  //    95f158536b00,92f259136b00,95f158536b00,92f259136b00,95f158536b00,92f259136b00,95f158536b00,
  //    92f259136b00,95f158536b00,92f259136b00,95f158536b00,92f259136b00,95f158536b00,92f259136b00,
  //    95f158536b00,92f259136b00,95f158536700,92f259136700,95f158550100,92f259150100,95f158535e00,
  //    92f259135e00,95f158535a00,92f259135a00,95f158535200,92f259135200,95f158534700,92f259134700,
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endmodule
