// Digital circuit XRAM.dig as structural Verilog
// stop ouput clock if input S  is high. if go is 1, clock will ouput normally.
module XRAM (
  input  CLK,
  input  [15:0] A,
  input  WE,
  input  nOE,
  output [7:0] O
);

  wire and_1_out, delay_1_out, delay_3_out, nand_1_out, not_1_out;
  wire [7:0] driver_2_out, driverinvsel_1_out, XRAM_d;
  wire [15:0] delay_2_out;

  Delay delay_1 (.in(CLK), .out(delay_1_out));
  not not_1 (not_1_out, delay_1_out);
  and and_1 (and_1_out, CLK, not_1_out);
  nand nand_1 (nand_1_out, WE, and_1_out);
  Delay #(.Bits(16), .delayTime(2)) delay_2 (.in(A), .out(delay_2_out));
  Delay #(.delayTime(2)) delay_3 (.in(nOE), .out(delay_3_out));
  RAMSinglePortSel #(.AddrBits(16), .isProgramMemory("true"), .Bits(8)) XRAM (
    .A(delay_2_out), .CS(~1'b0), .WE(~nand_1_out), .OE(~delay_3_out), .D(XRAM_d));
  assign driverinvsel_1_out = ~nOE ? XRAM_d : 8'bz;  // DriverInvSel driverinvsel_1
  assign XRAM_d = WE ? driver_2_out : 8'bz;  // Driver driver_1
  assign O = ~nOE ? driverinvsel_1_out : 8'bz;  // DriverInvSel driverinvsel_2
  assign driver_2_out = WE ? O : 8'bz;  // Driver driver_2

  // Notes on the sheet:
  //   A: address
  //   6116
  //   wait for the clock
  //   wait for the clock too
endmodule
