// Digital circuit reg, sync clear.dig as structural Verilog
module reg__sync_clear (
  input  [7:0] D,
  input  CLK,
  input  CLR,
  input  nLE,
  output [7:0] Q
);

  wire or_1_out;
  wire [7:0] multiplexer_1_out;

  or or_1 (or_1_out, CLR, ~nLE);  // Or
  Multiplexer #(.Bits(8), .generic("this.Bits = int(args.Bits);")) multiplexer_1 (
    .sel(CLR), .in_0(D), .in_1({8{1'b0}}), .out(multiplexer_1_out));
  Register #(.Bits(8), .generic("this.Bits = int(args.Bits);")) register_1 (
    .D(multiplexer_1_out), .C(CLK), .en(or_1_out), .Q(Q));

  // Notes on the sheet:
  //   D: Input pin of the data word to be stored.
  //   CLK: Clock input. A rising edge stores the value at the D pin.
  //   Q: Returns the stored value.
  //   CLR: sync clear pin. Reset value to zero when raise edge at CLK pin and this pin is high, higher priority than LE.
  //   nLE: Enable pin. Storing a value works only if this pin is set low.
endmodule
