// Digital circuit reg-file.dig as structural Verilog
module reg_file (
  input  CLK,
  input  [7:0] D,
  input  [3:0] RS,
  input  LE,
  input  CPF,
  output [7:0] Q,
  output PFF
);

  wire and_1_out, and_2_out, comparator_1_eq, comparator_2_eq, xor_1_out;
  wire [3:0] bitcount_1_out;
  wire [7:0] RFA_q, RFPSW_q;

  Comparator #(.Bits(4)) comparator_1 (.a(RS), .b(4'b0101), .eq(comparator_1_eq));  // open: gt, lt
  Comparator #(.Bits(4)) comparator_2 (.a(RS), .b(4'b0110), .eq(comparator_2_eq));  // open: gt, lt
  RAMDualPort #(.AddrBits(4), .Bits(8)) RF (.A(RS), .Din(D), .str(LE), .C(CLK), .ld(1'b1), .D(Q));
  and and_1 (and_1_out, comparator_1_eq, LE);
  and and_2 (and_2_out, comparator_2_eq, LE);
  Register #(.Bits(8)) RFPSW (.D(D), .C(CLK), .en(and_1_out), .Q(RFPSW_q));
  Register #(.Bits(8)) RFA (.D(D), .C(CLK), .en(and_2_out), .Q(RFA_q));
  BitCount #(.Bits(8)) bitcount_1 (.in(RFA_q), .out(bitcount_1_out));
  xor xor_1 (xor_1_out, RFPSW_q[0], bitcount_1_out[0]);
  and and_3 (PFF, xor_1_out, CPF);

  // Notes on the sheet:
  //   CPF: check PF
endmodule
