// Digital circuit reg.dig as structural Verilog
module \reg  (
  input  [7:0] D,
  input  CLK,
  input  nWE,
  input  [7:0] SETB,
  input  [7:0] nCLRB,
  input  nRST,
  output [7:0] Q
);

  wire [7:0] and_1_out, multiplexer_1_out, multiplexer_2_out, or_1_out;

  Multiplexer #(.Bits(8), .generic("this.Bits = int(args.Bits);")) multiplexer_1 (
    .sel(nWE), .in_0(D), .in_1(Q), .out(multiplexer_1_out));
  Multiplexer #(.Bits(8), .generic("this.Bits = int(args.Bits);")) multiplexer_2 (
    .sel(nRST), .in_0({8{1'b0}}), .in_1({8{1'b1}}), .out(multiplexer_2_out));
  assign or_1_out = multiplexer_1_out | SETB;  // Or or_1, 8 bits wide
  assign and_1_out = or_1_out & nCLRB & multiplexer_2_out;  // And and_1, 8 bits wide
  Register #(.Bits(8), .generic("this.Bits = int(args.Bits);")) register_1 (.D(and_1_out), .C(CLK), .en(1'b1), .Q(Q));

  // Notes on the sheet:
  //   D: Input pin of the data word to be stored.
  //   CLK: Clock input. A rising edge stores the value at the D pin.
  //   Q: Returns the stored value.
  //   nWE: Enable pin. Storing a value works only if this pin is set low., default 1
  //   SETB: set REG[n] to 1 if  SETB[n] is 1
  //   nCLRB: set REG[n] to 0 if  CLRB[n] is 0, default 255
  //   nRST: reset all, default 1
endmodule
