// Digital circuit reg4clr.dig as structural Verilog
module reg4clr (
  input  [3:0] D,
  input  CLK,
  input  CLR,
  input  LE,
  output [3:0] Q
);

  wire or_1_out;
  wire [3:0] multiplexer_1_out;

  Multiplexer #(.Bits(4)) multiplexer_1 (.sel(CLR), .in_0(D), .in_1(4'b0000), .out(multiplexer_1_out));
  or or_1 (or_1_out, CLR, LE);
  Register #(.Bits(4)) register_1 (.D(multiplexer_1_out), .C(CLK), .en(or_1_out), .Q(Q));
endmodule
