// Digital circuit reg8clr.dig as structural Verilog
module reg8clr (
  input  [7:0] D,
  input  CLK,
  input  CLR,
  input  LE,
  output [7:0] Q
);

  reg4clr reg4clr_1 (.D(D[3:0]), .CLK(CLK), .CLR(CLR), .LE(LE), .Q(Q[3:0]));
  reg4clr reg4clr_2 (.D(D[7:4]), .CLK(CLK), .CLR(CLR), .LE(LE), .Q(Q[7:4]));
endmodule
